// Logisim project 209127612_matmul.circ as structural Verilog: 11 circuits, main circuit matmul
module matmul (
  input  [7:0] x_row_0,
  input  [7:0] x_row_1,
  input  [7:0] x_row_2,
  input  [7:0] x_row_3,
  input  [7:0] x_row_4,
  input  [7:0] x_row_5,
  input  [7:0] x_row_6,
  input  [7:0] x_row_7,
  input  [7:0] y_row_0,
  input  [7:0] y_row_1,
  input  [7:0] y_row_2,
  input  [7:0] y_row_3,
  input  [7:0] y_row_4,
  input  [7:0] y_row_5,
  input  [7:0] y_row_6,
  input  [7:0] y_row_7,
  output [7:0] z_row_0,
  output [7:0] z_row_1,
  output [7:0] z_row_2,
  output [7:0] z_row_3,
  output [7:0] z_row_4,
  output [7:0] z_row_5,
  output [7:0] z_row_6,
  output [7:0] z_row_7
);

  wire [7:0] y_col_0, y_col_1, y_col_2, y_col_3, y_col_4, y_col_5, y_col_6, y_col_7;

  matmul_step_2 matmul_step_2_1 (
    .row(x_row_0), .col_0(y_col_0), .col_1(y_col_1), .col_2(y_col_2), .col_3(y_col_3), .col_4(y_col_4),
    .col_5(y_col_5), .col_6(y_col_6), .col_7(y_col_7), .product_row(z_row_0));
  matmul_step_2 matmul_step_2_2 (
    .row(x_row_1), .col_0(y_col_0), .col_1(y_col_1), .col_2(y_col_2), .col_3(y_col_3), .col_4(y_col_4),
    .col_5(y_col_5), .col_6(y_col_6), .col_7(y_col_7), .product_row(z_row_1));
  matmul_step_2 matmul_step_2_3 (
    .row(x_row_6), .col_0(y_col_0), .col_1(y_col_1), .col_2(y_col_2), .col_3(y_col_3), .col_4(y_col_4),
    .col_5(y_col_5), .col_6(y_col_6), .col_7(y_col_7), .product_row(z_row_6));
  DotMatrix #(.inputtype("row"), .matrixcols(8), .matrixrows(8)) dotmatrix_1 (
    .row0(x_row_0), .row1(x_row_1), .row2(x_row_2), .row3(x_row_3), .row4(x_row_4), .row5(x_row_5),
    .row6(x_row_6), .row7(x_row_7));
  DotMatrix #(.inputtype("row"), .matrixcols(8), .matrixrows(8)) dotmatrix_2 (
    .row0(y_row_0), .row1(y_row_1), .row2(y_row_2), .row3(y_row_3), .row4(y_row_4), .row5(y_row_5),
    .row6(y_row_6), .row7(y_row_7));
  transpose transpose_1 (
    .row_0(y_row_0), .row_1(y_row_1), .row_2(y_row_2), .row_3(y_row_3), .row_4(y_row_4), .row_5(y_row_5),
    .row_6(y_row_6), .row_7(y_row_7), .column_0(y_col_0), .column_1(y_col_1), .column_2(y_col_2),
    .column_3(y_col_3), .column_4(y_col_4), .column_5(y_col_5), .column_6(y_col_6), .column_7(y_col_7));
  matmul_step_2 matmul_step_2_4 (
    .row(x_row_2), .col_0(y_col_0), .col_1(y_col_1), .col_2(y_col_2), .col_3(y_col_3), .col_4(y_col_4),
    .col_5(y_col_5), .col_6(y_col_6), .col_7(y_col_7), .product_row(z_row_2));
  matmul_step_2 matmul_step_2_5 (
    .row(x_row_3), .col_0(y_col_0), .col_1(y_col_1), .col_2(y_col_2), .col_3(y_col_3), .col_4(y_col_4),
    .col_5(y_col_5), .col_6(y_col_6), .col_7(y_col_7), .product_row(z_row_3));
  matmul_step_2 matmul_step_2_6 (
    .row(x_row_7), .col_0(y_col_0), .col_1(y_col_1), .col_2(y_col_2), .col_3(y_col_3), .col_4(y_col_4),
    .col_5(y_col_5), .col_6(y_col_6), .col_7(y_col_7), .product_row(z_row_7));
  DotMatrix #(.inputtype("row"), .matrixcols(8), .matrixrows(8)) dotmatrix_3 (
    .row0(z_row_0), .row1(z_row_1), .row2(z_row_2), .row3(z_row_3), .row4(z_row_4), .row5(z_row_5),
    .row6(z_row_6), .row7(z_row_7));
  matmul_step_2 matmul_step_2_7 (
    .row(x_row_4), .col_0(y_col_0), .col_1(y_col_1), .col_2(y_col_2), .col_3(y_col_3), .col_4(y_col_4),
    .col_5(y_col_5), .col_6(y_col_6), .col_7(y_col_7), .product_row(z_row_4));
  matmul_step_2 matmul_step_2_8 (
    .row(x_row_5), .col_0(y_col_0), .col_1(y_col_1), .col_2(y_col_2), .col_3(y_col_3), .col_4(y_col_4),
    .col_5(y_col_5), .col_6(y_col_6), .col_7(y_col_7), .product_row(z_row_5));
endmodule

module transpose (
  input  [7:0] row_0,
  input  [7:0] row_1,
  input  [7:0] row_2,
  input  [7:0] row_3,
  input  [7:0] row_4,
  input  [7:0] row_5,
  input  [7:0] row_6,
  input  [7:0] row_7,
  output [7:0] column_0,
  output [7:0] column_1,
  output [7:0] column_2,
  output [7:0] column_3,
  output [7:0] column_4,
  output [7:0] column_5,
  output [7:0] column_6,
  output [7:0] column_7
);

  extract_col extract_col_1 (
    .in_1(3'b000), .row_0(row_0), .row_1(row_1), .row_2(row_2), .row_3(row_3), .row_4(row_4), .row_5(row_5),
    .row_6(row_6), .row_7(row_7), .b(column_0));
  extract_col extract_col_2 (
    .in_1(3'b100), .row_0(row_0), .row_1(row_1), .row_2(row_2), .row_3(row_3), .row_4(row_4), .row_5(row_5),
    .row_6(row_6), .row_7(row_7), .b(column_4));
  extract_col extract_col_3 (
    .in_1(3'b001), .row_0(row_0), .row_1(row_1), .row_2(row_2), .row_3(row_3), .row_4(row_4), .row_5(row_5),
    .row_6(row_6), .row_7(row_7), .b(column_1));
  extract_col extract_col_4 (
    .in_1(3'b101), .row_0(row_0), .row_1(row_1), .row_2(row_2), .row_3(row_3), .row_4(row_4), .row_5(row_5),
    .row_6(row_6), .row_7(row_7), .b(column_5));
  extract_col extract_col_5 (
    .in_1(3'b010), .row_0(row_0), .row_1(row_1), .row_2(row_2), .row_3(row_3), .row_4(row_4), .row_5(row_5),
    .row_6(row_6), .row_7(row_7), .b(column_2));
  extract_col extract_col_6 (
    .in_1(3'b110), .row_0(row_0), .row_1(row_1), .row_2(row_2), .row_3(row_3), .row_4(row_4), .row_5(row_5),
    .row_6(row_6), .row_7(row_7), .b(column_6));
  extract_col extract_col_7 (
    .in_1(3'b011), .row_0(row_0), .row_1(row_1), .row_2(row_2), .row_3(row_3), .row_4(row_4), .row_5(row_5),
    .row_6(row_6), .row_7(row_7), .b(column_3));
  extract_col extract_col_8 (
    .in_1(3'b111), .row_0(row_0), .row_1(row_1), .row_2(row_2), .row_3(row_3), .row_4(row_4), .row_5(row_5),
    .row_6(row_6), .row_7(row_7), .b(column_7));
endmodule

module extract_col (
  input  [2:0] in_1,
  input  [7:0] row_0,
  input  [7:0] row_1,
  input  [7:0] row_2,
  input  [7:0] row_3,
  input  [7:0] row_4,
  input  [7:0] row_5,
  input  [7:0] row_6,
  input  [7:0] row_7,
  output [7:0] b
);

  wire [2:0] not_1_out, not_2_out, not_3_out, not_4_out, not_5_out, not_6_out, not_7_out, not_8_out;

  BitSelector bitselector_1 (.in(row_0), .out(b[7]), .sel(not_1_out));
  assign not_1_out = ~in_1;  // NOT_Gate not_1, 3 bits wide
  BitSelector bitselector_2 (.in(row_1), .out(b[6]), .sel(not_2_out));
  assign not_2_out = ~in_1;  // NOT_Gate not_2, 3 bits wide
  BitSelector bitselector_3 (.in(row_2), .out(b[5]), .sel(not_3_out));
  assign not_3_out = ~in_1;  // NOT_Gate not_3, 3 bits wide
  BitSelector bitselector_4 (.in(row_3), .out(b[4]), .sel(not_4_out));
  assign not_4_out = ~in_1;  // NOT_Gate not_4, 3 bits wide
  BitSelector bitselector_5 (.in(row_4), .out(b[3]), .sel(not_5_out));
  assign not_5_out = ~in_1;  // NOT_Gate not_5, 3 bits wide
  BitSelector bitselector_6 (.in(row_5), .out(b[2]), .sel(not_6_out));
  assign not_6_out = ~in_1;  // NOT_Gate not_6, 3 bits wide
  BitSelector bitselector_7 (.in(row_6), .out(b[1]), .sel(not_7_out));
  assign not_7_out = ~in_1;  // NOT_Gate not_7, 3 bits wide
  BitSelector bitselector_8 (.in(row_7), .out(b[0]), .sel(not_8_out));
  assign not_8_out = ~in_1;  // NOT_Gate not_8, 3 bits wide

  // Other names for the same wires on the sheet: col[7:0] = b; col_num[2:0] = in_1
endmodule

module matmul_step_1 (
  input  [7:0] row,
  input  [7:0] col,
  output \output 
);

  wire and_1_out, and_2_out, and_3_out, and_4_out, and_5_out, and_6_out, and_7_out, and_8_out, or_1_out,
       or_2_out, or_3_out, or_4_out, or_5_out, or_6_out;

  and and_1 (and_1_out, row[0], col[0]);
  and and_2 (and_2_out, row[1], col[1]);
  and and_3 (and_3_out, row[2], col[2]);
  and and_4 (and_4_out, row[3], col[3]);
  and and_5 (and_5_out, row[4], col[4]);
  and and_6 (and_6_out, row[5], col[5]);
  and and_7 (and_7_out, row[6], col[6]);
  and and_8 (and_8_out, row[7], col[7]);
  or or_1 (or_1_out, and_1_out, and_2_out);
  or or_2 (or_2_out, and_3_out, and_4_out);
  or or_3 (or_3_out, and_5_out, and_6_out);
  or or_4 (or_4_out, and_7_out, and_8_out);
  or or_5 (or_5_out, or_1_out, or_2_out);
  or or_6 (or_6_out, or_3_out, or_4_out);
  or or_7 (\output , or_5_out, or_6_out);

  // Other names for the same wires on the sheet: y00 = col[0]; y01 = col[1]; y02 = col[2]; y03 = col[3]; y04 = col[4];
  //   y05 = col[5]; y06 = col[6]; y07 = col[7]; x00 = row[0]; x01 = row[1]; x02 = row[2]; x03 = row[3]; x04 = row[4];
  //   x05 = row[5]; x06 = row[6]; x07 = row[7]
endmodule

module matmul_step_2 (
  input  [7:0] row,
  input  [7:0] col_0,
  input  [7:0] col_1,
  input  [7:0] col_2,
  input  [7:0] col_3,
  input  [7:0] col_4,
  input  [7:0] col_5,
  input  [7:0] col_6,
  input  [7:0] col_7,
  output [7:0] product_row
);

  matmul_step_1 matmul_step_1_1 (.row(row), .col(col_7), .\output (product_row[0]));
  matmul_step_1 matmul_step_1_2 (.row(row), .col(col_6), .\output (product_row[1]));
  matmul_step_1 matmul_step_1_3 (.row(row), .col(col_5), .\output (product_row[2]));
  matmul_step_1 matmul_step_1_4 (.row(row), .col(col_4), .\output (product_row[3]));
  matmul_step_1 matmul_step_1_5 (.row(row), .col(col_3), .\output (product_row[4]));
  matmul_step_1 matmul_step_1_6 (.row(row), .col(col_2), .\output (product_row[5]));
  matmul_step_1 matmul_step_1_7 (.row(row), .col(col_1), .\output (product_row[6]));
  matmul_step_1 matmul_step_1_8 (.row(row), .col(col_0), .\output (product_row[7]));
endmodule

module bitwise_or_8_8 (
  input  [7:0] x_row_0,
  input  [7:0] x_row_1,
  input  [7:0] x_row_2,
  input  [7:0] x_row_3,
  input  [7:0] x_row_4,
  input  [7:0] x_row_5,
  input  [7:0] x_row_6,
  input  [7:0] x_row_7,
  input  [7:0] y_row_0,
  input  [7:0] y_row_1,
  input  [7:0] y_row_2,
  input  [7:0] y_row_3,
  input  [7:0] y_row_4,
  input  [7:0] y_row_5,
  input  [7:0] y_row_6,
  input  [7:0] y_row_7,
  output [7:0] z_row_0,
  output [7:0] z_row_1,
  output [7:0] z_row_2,
  output [7:0] z_row_3,
  output [7:0] z_row_4,
  output [7:0] z_row_5,
  output [7:0] z_row_6,
  output [7:0] z_row_7
);

  DotMatrix #(.inputtype("row"), .matrixcols(8), .matrixrows(8)) dotmatrix_1 (
    .row0(x_row_0), .row1(x_row_1), .row2(x_row_2), .row3(x_row_3), .row4(x_row_4), .row5(x_row_5),
    .row6(x_row_6), .row7(x_row_7));
  DotMatrix #(.inputtype("row"), .matrixcols(8), .matrixrows(8)) dotmatrix_2 (
    .row0(y_row_0), .row1(y_row_1), .row2(y_row_2), .row3(y_row_3), .row4(y_row_4), .row5(y_row_5),
    .row6(y_row_6), .row7(y_row_7));
  or or_1 (z_row_0[0], x_row_0[0], y_row_0[0]);
  or or_2 (z_row_0[1], x_row_0[1], y_row_0[1]);
  or or_3 (z_row_0[2], x_row_0[2], y_row_0[2]);
  or or_4 (z_row_0[3], x_row_0[3], y_row_0[3]);
  or or_5 (z_row_0[4], x_row_0[4], y_row_0[4]);
  or or_6 (z_row_0[5], x_row_0[5], y_row_0[5]);
  or or_7 (z_row_0[6], x_row_0[6], y_row_0[6]);
  or or_8 (z_row_0[7], x_row_0[7], y_row_0[7]);
  or or_9 (z_row_1[0], x_row_1[0], y_row_1[0]);
  or or_10 (z_row_1[1], x_row_1[1], y_row_1[1]);
  or or_11 (z_row_1[2], x_row_1[2], y_row_1[2]);
  or or_12 (z_row_1[3], x_row_1[3], y_row_1[3]);
  or or_13 (z_row_1[4], x_row_1[4], y_row_1[4]);
  or or_14 (z_row_1[5], x_row_1[5], y_row_1[5]);
  or or_15 (z_row_1[6], x_row_1[6], y_row_1[6]);
  or or_16 (z_row_1[7], x_row_1[7], y_row_1[7]);
  or or_17 (z_row_2[0], x_row_2[0], y_row_2[0]);
  or or_18 (z_row_2[1], x_row_2[1], y_row_2[1]);
  or or_19 (z_row_2[2], x_row_2[2], y_row_2[2]);
  or or_20 (z_row_2[3], x_row_2[3], y_row_2[3]);
  or or_21 (z_row_2[4], x_row_2[4], y_row_2[4]);
  or or_22 (z_row_2[5], x_row_2[5], y_row_2[5]);
  or or_23 (z_row_2[6], x_row_2[6], y_row_2[6]);
  or or_24 (z_row_2[7], x_row_2[7], y_row_2[7]);
  or or_25 (z_row_3[0], x_row_3[0], y_row_3[0]);
  or or_26 (z_row_3[1], x_row_3[1], y_row_3[1]);
  or or_27 (z_row_3[2], x_row_3[2], y_row_3[2]);
  or or_28 (z_row_3[3], x_row_3[3], y_row_3[3]);
  or or_29 (z_row_3[4], x_row_3[4], y_row_3[4]);
  or or_30 (z_row_3[5], x_row_3[5], y_row_3[5]);
  or or_31 (z_row_3[6], x_row_3[6], y_row_3[6]);
  or or_32 (z_row_3[7], x_row_3[7], y_row_3[7]);
  DotMatrix #(.inputtype("row"), .matrixcols(8), .matrixrows(8)) dotmatrix_3 (
    .row0(z_row_0), .row1(z_row_1), .row2(z_row_2), .row3(z_row_3), .row4(z_row_4), .row5(z_row_5),
    .row6(z_row_6), .row7(z_row_7));
  or or_33 (z_row_4[0], x_row_4[0], y_row_4[0]);
  or or_34 (z_row_4[1], x_row_4[1], y_row_4[1]);
  or or_35 (z_row_4[2], x_row_4[2], y_row_4[2]);
  or or_36 (z_row_4[3], x_row_4[3], y_row_4[3]);
  or or_37 (z_row_4[4], x_row_4[4], y_row_4[4]);
  or or_38 (z_row_4[5], x_row_4[5], y_row_4[5]);
  or or_39 (z_row_4[6], x_row_4[6], y_row_4[6]);
  or or_40 (z_row_4[7], x_row_4[7], y_row_4[7]);
  or or_41 (z_row_5[0], x_row_5[0], y_row_5[0]);
  or or_42 (z_row_5[1], x_row_5[1], y_row_5[1]);
  or or_43 (z_row_5[2], x_row_5[2], y_row_5[2]);
  or or_44 (z_row_5[3], x_row_5[3], y_row_5[3]);
  or or_45 (z_row_5[4], x_row_5[4], y_row_5[4]);
  or or_46 (z_row_5[5], x_row_5[5], y_row_5[5]);
  or or_47 (z_row_5[6], x_row_5[6], y_row_5[6]);
  or or_48 (z_row_5[7], x_row_5[7], y_row_5[7]);
  or or_49 (z_row_6[0], x_row_6[0], y_row_6[0]);
  or or_50 (z_row_6[1], x_row_6[1], y_row_6[1]);
  or or_51 (z_row_6[2], x_row_6[2], y_row_6[2]);
  or or_52 (z_row_6[3], x_row_6[3], y_row_6[3]);
  or or_53 (z_row_6[4], x_row_6[4], y_row_6[4]);
  or or_54 (z_row_6[5], x_row_6[5], y_row_6[5]);
  or or_55 (z_row_6[6], x_row_6[6], y_row_6[6]);
  or or_56 (z_row_6[7], x_row_6[7], y_row_6[7]);
  or or_57 (z_row_7[0], x_row_7[0], y_row_7[0]);
  or or_58 (z_row_7[1], x_row_7[1], y_row_7[1]);
  or or_59 (z_row_7[2], x_row_7[2], y_row_7[2]);
  or or_60 (z_row_7[3], x_row_7[3], y_row_7[3]);
  or or_61 (z_row_7[4], x_row_7[4], y_row_7[4]);
  or or_62 (z_row_7[5], x_row_7[5], y_row_7[5]);
  or or_63 (z_row_7[6], x_row_7[6], y_row_7[6]);
  or or_64 (z_row_7[7], x_row_7[7], y_row_7[7]);

  // Other names for the same wires on the sheet: x00 = x_row_0[0]; x01 = x_row_0[1]; x02 = x_row_0[2];
  //   x03 = x_row_0[3]; x04 = x_row_0[4]; x05 = x_row_0[5]; x06 = x_row_0[6]; x07 = x_row_0[7]; x10 = x_row_1[0];
  //   x11 = x_row_1[1]; x12 = x_row_1[2]; x13 = x_row_1[3]; x14 = x_row_1[4]; x15 = x_row_1[5]; x16 = x_row_1[6];
  //   x17 = x_row_1[7]; x20 = x_row_2[0]; x21 = x_row_2[1]; x22 = x_row_2[2]; x23 = x_row_2[3]; x24 = x_row_2[4];
  //   x25 = x_row_2[5]; x26 = x_row_2[6]; x27 = x_row_2[7]; x30 = x_row_3[0]; x31 = x_row_3[1]; x32 = x_row_3[2];
  //   x33 = x_row_3[3]; x34 = x_row_3[4]; x35 = x_row_3[5]; x36 = x_row_3[6]; x37 = x_row_3[7]; x40 = x_row_4[0];
  //   x41 = x_row_4[1]; x42 = x_row_4[2]; x43 = x_row_4[3]; x44 = x_row_4[4]; x45 = x_row_4[5]; x46 = x_row_4[6];
  //   x47 = x_row_4[7]; x50 = x_row_5[0]; x51 = x_row_5[1]; x52 = x_row_5[2]; x53 = x_row_5[3]; x54 = x_row_5[4];
  //   x55 = x_row_5[5]; x56 = x_row_5[6]; x57 = x_row_5[7]; x60 = x_row_6[0]; x61 = x_row_6[1]; x62 = x_row_6[2];
  //   x63 = x_row_6[3]; x64 = x_row_6[4]; x65 = x_row_6[5]; x66 = x_row_6[6]; x67 = x_row_6[7]; x70 = x_row_7[0];
  //   x71 = x_row_7[1]; x72 = x_row_7[2]; x73 = x_row_7[3]; x74 = x_row_7[4]; x75 = x_row_7[5]; x76 = x_row_7[6];
  //   x77 = x_row_7[7]; y00 = y_row_0[0]; y01 = y_row_0[1]; y02 = y_row_0[2]; y03 = y_row_0[3]; y04 = y_row_0[4];
  //   y05 = y_row_0[5]; y06 = y_row_0[6]; y07 = y_row_0[7]; y10 = y_row_1[0]; y11 = y_row_1[1]; y12 = y_row_1[2];
  //   y13 = y_row_1[3]; y14 = y_row_1[4]; y15 = y_row_1[5]; y16 = y_row_1[6]; y17 = y_row_1[7]; y20 = y_row_2[0];
  //   y21 = y_row_2[1]; y22 = y_row_2[2]; y23 = y_row_2[3]; y24 = y_row_2[4]; y25 = y_row_2[5]; y26 = y_row_2[6];
  //   y27 = y_row_2[7]; y30 = y_row_3[0]; y31 = y_row_3[1]; y32 = y_row_3[2]; y33 = y_row_3[3]; y34 = y_row_3[4];
  //   y35 = y_row_3[5]; y36 = y_row_3[6]; y37 = y_row_3[7]; y40 = y_row_4[0]; y41 = y_row_4[1]; y42 = y_row_4[2];
  //   y43 = y_row_4[3]; y44 = y_row_4[4]; y45 = y_row_4[5]; y46 = y_row_4[6]; y47 = y_row_4[7]; y50 = y_row_5[0];
  //   y51 = y_row_5[1]; y52 = y_row_5[2]; y53 = y_row_5[3]; y54 = y_row_5[4]; y55 = y_row_5[5]; y56 = y_row_5[6];
  //   y57 = y_row_5[7]; y60 = y_row_6[0]; y61 = y_row_6[1]; y62 = y_row_6[2]; y63 = y_row_6[3]; y64 = y_row_6[4];
  //   y65 = y_row_6[5]; y66 = y_row_6[6]; y67 = y_row_6[7]; y70 = y_row_7[0]; y71 = y_row_7[1]; y72 = y_row_7[2];
  //   y73 = y_row_7[3]; y74 = y_row_7[4]; y75 = y_row_7[5]; y76 = y_row_7[6]; y77 = y_row_7[7]
endmodule

module is_connected (
  input  [7:0] x_row_0,
  input  [7:0] x_row_1,
  input  [7:0] x_row_2,
  input  [7:0] x_row_3,
  input  [7:0] x_row_4,
  input  [7:0] x_row_5,
  input  [7:0] x_row_6,
  input  [7:0] x_row_7,
  output is_connected
);

  wire [7:0] bitwise_or_8_8_1_z_row_0, bitwise_or_8_8_1_z_row_1, bitwise_or_8_8_1_z_row_2,
       bitwise_or_8_8_1_z_row_3, bitwise_or_8_8_1_z_row_4, bitwise_or_8_8_1_z_row_5,
       bitwise_or_8_8_1_z_row_6, bitwise_or_8_8_1_z_row_7, bitwise_or_8_8_2_z_row_0,
       bitwise_or_8_8_2_z_row_1, bitwise_or_8_8_2_z_row_2, bitwise_or_8_8_2_z_row_3,
       bitwise_or_8_8_2_z_row_4, bitwise_or_8_8_2_z_row_5, bitwise_or_8_8_2_z_row_6,
       bitwise_or_8_8_2_z_row_7, bitwise_or_8_8_3_z_row_0, bitwise_or_8_8_3_z_row_1,
       bitwise_or_8_8_3_z_row_2, bitwise_or_8_8_3_z_row_3, bitwise_or_8_8_3_z_row_4,
       bitwise_or_8_8_3_z_row_5, bitwise_or_8_8_3_z_row_6, bitwise_or_8_8_3_z_row_7,
       bitwise_or_8_8_4_z_row_0, bitwise_or_8_8_4_z_row_1, bitwise_or_8_8_4_z_row_2,
       bitwise_or_8_8_4_z_row_3, bitwise_or_8_8_4_z_row_4, bitwise_or_8_8_4_z_row_5,
       bitwise_or_8_8_4_z_row_6, bitwise_or_8_8_4_z_row_7, bitwise_or_8_8_5_z_row_0,
       bitwise_or_8_8_5_z_row_1, bitwise_or_8_8_5_z_row_2, bitwise_or_8_8_5_z_row_3,
       bitwise_or_8_8_5_z_row_4, bitwise_or_8_8_5_z_row_5, bitwise_or_8_8_5_z_row_6,
       bitwise_or_8_8_5_z_row_7, bitwise_or_8_8_6_z_row_0, bitwise_or_8_8_6_z_row_1,
       bitwise_or_8_8_6_z_row_2, bitwise_or_8_8_6_z_row_3, bitwise_or_8_8_6_z_row_4,
       bitwise_or_8_8_6_z_row_5, bitwise_or_8_8_6_z_row_6, bitwise_or_8_8_6_z_row_7,
       bitwise_or_8_8_7_z_row_0, bitwise_or_8_8_7_z_row_1, bitwise_or_8_8_7_z_row_2,
       bitwise_or_8_8_7_z_row_3, bitwise_or_8_8_7_z_row_4, bitwise_or_8_8_7_z_row_5,
       bitwise_or_8_8_7_z_row_6, bitwise_or_8_8_7_z_row_7, x1_row_0, x1_row_1, x1_row_2, x1_row_3, x1_row_4,
       x1_row_5, x1_row_6, x1_row_7, x2_row_0, x2_row_1, x2_row_2, x2_row_3, x2_row_4, x2_row_5, x2_row_6,
       x2_row_7, x3_row_0, x3_row_1, x3_row_2, x3_row_3, x3_row_4, x3_row_5, x3_row_6, x3_row_7, x4_row_0,
       x4_row_1, x4_row_2, x4_row_3, x4_row_4, x4_row_5, x4_row_6, x4_row_7, x5_row_0, x5_row_1, x5_row_2,
       x5_row_3, x5_row_4, x5_row_5, x5_row_6, x5_row_7, x6_row_0, x6_row_1, x6_row_2, x6_row_3, x6_row_4,
       x6_row_5, x6_row_6, x6_row_7;

  matmul matmul_1 (
    .x_row_0(x_row_0), .x_row_1(x_row_1), .x_row_2(x_row_2), .x_row_3(x_row_3), .x_row_4(x_row_4),
    .x_row_5(x_row_5), .x_row_6(x_row_6), .x_row_7(x_row_7), .y_row_0(x_row_0), .y_row_1(x_row_1),
    .y_row_2(x_row_2), .y_row_3(x_row_3), .y_row_4(x_row_4), .y_row_5(x_row_5), .y_row_6(x_row_6),
    .y_row_7(x_row_7), .z_row_0(x1_row_0), .z_row_1(x1_row_1), .z_row_2(x1_row_2), .z_row_3(x1_row_3),
    .z_row_4(x1_row_4), .z_row_5(x1_row_5), .z_row_6(x1_row_6), .z_row_7(x1_row_7));
  matmul matmul_2 (
    .x_row_0(x1_row_0), .x_row_1(x1_row_1), .x_row_2(x1_row_2), .x_row_3(x1_row_3), .x_row_4(x1_row_4),
    .x_row_5(x1_row_5), .x_row_6(x1_row_6), .x_row_7(x1_row_7), .y_row_0(x_row_0), .y_row_1(x_row_1),
    .y_row_2(x_row_2), .y_row_3(x_row_3), .y_row_4(x_row_4), .y_row_5(x_row_5), .y_row_6(x_row_6),
    .y_row_7(x_row_7), .z_row_0(x2_row_0), .z_row_1(x2_row_1), .z_row_2(x2_row_2), .z_row_3(x2_row_3),
    .z_row_4(x2_row_4), .z_row_5(x2_row_5), .z_row_6(x2_row_6), .z_row_7(x2_row_7));
  matmul matmul_3 (
    .x_row_0(x2_row_0), .x_row_1(x2_row_1), .x_row_2(x2_row_2), .x_row_3(x2_row_3), .x_row_4(x2_row_4),
    .x_row_5(x2_row_5), .x_row_6(x2_row_6), .x_row_7(x2_row_7), .y_row_0(x_row_0), .y_row_1(x_row_1),
    .y_row_2(x_row_2), .y_row_3(x_row_3), .y_row_4(x_row_4), .y_row_5(x_row_5), .y_row_6(x_row_6),
    .y_row_7(x_row_7), .z_row_0(x3_row_0), .z_row_1(x3_row_1), .z_row_2(x3_row_2), .z_row_3(x3_row_3),
    .z_row_4(x3_row_4), .z_row_5(x3_row_5), .z_row_6(x3_row_6), .z_row_7(x3_row_7));
  matmul matmul_4 (
    .x_row_0(x3_row_0), .x_row_1(x3_row_1), .x_row_2(x3_row_2), .x_row_3(x3_row_3), .x_row_4(x3_row_4),
    .x_row_5(x3_row_5), .x_row_6(x3_row_6), .x_row_7(x3_row_7), .y_row_0(x_row_0), .y_row_1(x_row_1),
    .y_row_2(x_row_2), .y_row_3(x_row_3), .y_row_4(x_row_4), .y_row_5(x_row_5), .y_row_6(x_row_6),
    .y_row_7(x_row_7), .z_row_0(x4_row_0), .z_row_1(x4_row_1), .z_row_2(x4_row_2), .z_row_3(x4_row_3),
    .z_row_4(x4_row_4), .z_row_5(x4_row_5), .z_row_6(x4_row_6), .z_row_7(x4_row_7));
  matmul matmul_5 (
    .x_row_0(x4_row_0), .x_row_1(x4_row_1), .x_row_2(x4_row_2), .x_row_3(x4_row_3), .x_row_4(x4_row_4),
    .x_row_5(x4_row_5), .x_row_6(x4_row_6), .x_row_7(x4_row_7), .y_row_0(x_row_0), .y_row_1(x_row_1),
    .y_row_2(x_row_2), .y_row_3(x_row_3), .y_row_4(x_row_4), .y_row_5(x_row_5), .y_row_6(x_row_6),
    .y_row_7(x_row_7), .z_row_0(x5_row_0), .z_row_1(x5_row_1), .z_row_2(x5_row_2), .z_row_3(x5_row_3),
    .z_row_4(x5_row_4), .z_row_5(x5_row_5), .z_row_6(x5_row_6), .z_row_7(x5_row_7));
  matmul matmul_6 (
    .x_row_0(x5_row_0), .x_row_1(x5_row_1), .x_row_2(x5_row_2), .x_row_3(x5_row_3), .x_row_4(x5_row_4),
    .x_row_5(x5_row_5), .x_row_6(x5_row_6), .x_row_7(x5_row_7), .y_row_0(x_row_0), .y_row_1(x_row_1),
    .y_row_2(x_row_2), .y_row_3(x_row_3), .y_row_4(x_row_4), .y_row_5(x_row_5), .y_row_6(x_row_6),
    .y_row_7(x_row_7), .z_row_0(x6_row_0), .z_row_1(x6_row_1), .z_row_2(x6_row_2), .z_row_3(x6_row_3),
    .z_row_4(x6_row_4), .z_row_5(x6_row_5), .z_row_6(x6_row_6), .z_row_7(x6_row_7));
  DotMatrix #(.inputtype("row"), .matrixcols(8), .matrixrows(8)) dotmatrix_1 (
    .row0(x_row_0), .row1(x_row_1), .row2(x_row_2), .row3(x_row_3), .row4(x_row_4), .row5(x_row_5),
    .row6(x_row_6), .row7(x_row_7));
  bitwise_or_8_8 bitwise_or_8_8_1 (
    .x_row_0(x_row_0), .x_row_1(x_row_1), .x_row_2(x_row_2), .x_row_3(x_row_3), .x_row_4(x_row_4),
    .x_row_5(x_row_5), .x_row_6(x_row_6), .x_row_7(x_row_7), .y_row_0(x1_row_0), .y_row_1(x1_row_1),
    .y_row_2(x1_row_2), .y_row_3(x1_row_3), .y_row_4(x1_row_4), .y_row_5(x1_row_5), .y_row_6(x1_row_6),
    .y_row_7(x1_row_7), .z_row_0(bitwise_or_8_8_1_z_row_0), .z_row_1(bitwise_or_8_8_1_z_row_1),
    .z_row_2(bitwise_or_8_8_1_z_row_2), .z_row_3(bitwise_or_8_8_1_z_row_3),
    .z_row_4(bitwise_or_8_8_1_z_row_4), .z_row_5(bitwise_or_8_8_1_z_row_5),
    .z_row_6(bitwise_or_8_8_1_z_row_6), .z_row_7(bitwise_or_8_8_1_z_row_7));
  bitwise_or_8_8 bitwise_or_8_8_2 (
    .x_row_0(x2_row_0), .x_row_1(x2_row_1), .x_row_2(x2_row_2), .x_row_3(x2_row_3), .x_row_4(x2_row_4),
    .x_row_5(x2_row_5), .x_row_6(x2_row_6), .x_row_7(x2_row_7), .y_row_0(x3_row_0), .y_row_1(x3_row_1),
    .y_row_2(x3_row_2), .y_row_3(x3_row_3), .y_row_4(x3_row_4), .y_row_5(x3_row_5), .y_row_6(x3_row_6),
    .y_row_7(x3_row_7), .z_row_0(bitwise_or_8_8_2_z_row_0), .z_row_1(bitwise_or_8_8_2_z_row_1),
    .z_row_2(bitwise_or_8_8_2_z_row_2), .z_row_3(bitwise_or_8_8_2_z_row_3),
    .z_row_4(bitwise_or_8_8_2_z_row_4), .z_row_5(bitwise_or_8_8_2_z_row_5),
    .z_row_6(bitwise_or_8_8_2_z_row_6), .z_row_7(bitwise_or_8_8_2_z_row_7));
  bitwise_or_8_8 bitwise_or_8_8_3 (
    .x_row_0(x4_row_0), .x_row_1(x4_row_1), .x_row_2(x4_row_2), .x_row_3(x4_row_3), .x_row_4(x4_row_4),
    .x_row_5(x4_row_5), .x_row_6(x4_row_6), .x_row_7(x4_row_7), .y_row_0(x5_row_0), .y_row_1(x5_row_1),
    .y_row_2(x5_row_2), .y_row_3(x5_row_3), .y_row_4(x5_row_4), .y_row_5(x5_row_5), .y_row_6(x5_row_6),
    .y_row_7(x5_row_7), .z_row_0(bitwise_or_8_8_3_z_row_0), .z_row_1(bitwise_or_8_8_3_z_row_1),
    .z_row_2(bitwise_or_8_8_3_z_row_2), .z_row_3(bitwise_or_8_8_3_z_row_3),
    .z_row_4(bitwise_or_8_8_3_z_row_4), .z_row_5(bitwise_or_8_8_3_z_row_5),
    .z_row_6(bitwise_or_8_8_3_z_row_6), .z_row_7(bitwise_or_8_8_3_z_row_7));
  bitwise_or_8_8 bitwise_or_8_8_4 (
    .x_row_0(bitwise_or_8_8_1_z_row_0), .x_row_1(bitwise_or_8_8_1_z_row_1),
    .x_row_2(bitwise_or_8_8_1_z_row_2), .x_row_3(bitwise_or_8_8_1_z_row_3),
    .x_row_4(bitwise_or_8_8_1_z_row_4), .x_row_5(bitwise_or_8_8_1_z_row_5),
    .x_row_6(bitwise_or_8_8_1_z_row_6), .x_row_7(bitwise_or_8_8_1_z_row_7),
    .y_row_0(bitwise_or_8_8_2_z_row_0), .y_row_1(bitwise_or_8_8_2_z_row_1),
    .y_row_2(bitwise_or_8_8_2_z_row_2), .y_row_3(bitwise_or_8_8_2_z_row_3),
    .y_row_4(bitwise_or_8_8_2_z_row_4), .y_row_5(bitwise_or_8_8_2_z_row_5),
    .y_row_6(bitwise_or_8_8_2_z_row_6), .y_row_7(bitwise_or_8_8_2_z_row_7),
    .z_row_0(bitwise_or_8_8_4_z_row_0), .z_row_1(bitwise_or_8_8_4_z_row_1),
    .z_row_2(bitwise_or_8_8_4_z_row_2), .z_row_3(bitwise_or_8_8_4_z_row_3),
    .z_row_4(bitwise_or_8_8_4_z_row_4), .z_row_5(bitwise_or_8_8_4_z_row_5),
    .z_row_6(bitwise_or_8_8_4_z_row_6), .z_row_7(bitwise_or_8_8_4_z_row_7));
  bitwise_or_8_8 bitwise_or_8_8_5 (
    .x_row_0(bitwise_or_8_8_3_z_row_0), .x_row_1(bitwise_or_8_8_3_z_row_1),
    .x_row_2(bitwise_or_8_8_3_z_row_2), .x_row_3(bitwise_or_8_8_3_z_row_3),
    .x_row_4(bitwise_or_8_8_3_z_row_4), .x_row_5(bitwise_or_8_8_3_z_row_5),
    .x_row_6(bitwise_or_8_8_3_z_row_6), .x_row_7(bitwise_or_8_8_3_z_row_7), .y_row_0(x6_row_0),
    .y_row_1(x6_row_1), .y_row_2(x6_row_2), .y_row_3(x6_row_3), .y_row_4(x6_row_4), .y_row_5(x6_row_5),
    .y_row_6(x6_row_6), .y_row_7(x6_row_7), .z_row_0(bitwise_or_8_8_5_z_row_0),
    .z_row_1(bitwise_or_8_8_5_z_row_1), .z_row_2(bitwise_or_8_8_5_z_row_2),
    .z_row_3(bitwise_or_8_8_5_z_row_3), .z_row_4(bitwise_or_8_8_5_z_row_4),
    .z_row_5(bitwise_or_8_8_5_z_row_5), .z_row_6(bitwise_or_8_8_5_z_row_6), .z_row_7(bitwise_or_8_8_5_z_row_7));
  bitwise_or_8_8 bitwise_or_8_8_6 (
    .x_row_0(bitwise_or_8_8_4_z_row_0), .x_row_1(bitwise_or_8_8_4_z_row_1),
    .x_row_2(bitwise_or_8_8_4_z_row_2), .x_row_3(bitwise_or_8_8_4_z_row_3),
    .x_row_4(bitwise_or_8_8_4_z_row_4), .x_row_5(bitwise_or_8_8_4_z_row_5),
    .x_row_6(bitwise_or_8_8_4_z_row_6), .x_row_7(bitwise_or_8_8_4_z_row_7),
    .y_row_0(bitwise_or_8_8_5_z_row_0), .y_row_1(bitwise_or_8_8_5_z_row_1),
    .y_row_2(bitwise_or_8_8_5_z_row_2), .y_row_3(bitwise_or_8_8_5_z_row_3),
    .y_row_4(bitwise_or_8_8_5_z_row_4), .y_row_5(bitwise_or_8_8_5_z_row_5),
    .y_row_6(bitwise_or_8_8_5_z_row_6), .y_row_7(bitwise_or_8_8_5_z_row_7),
    .z_row_0(bitwise_or_8_8_6_z_row_0), .z_row_1(bitwise_or_8_8_6_z_row_1),
    .z_row_2(bitwise_or_8_8_6_z_row_2), .z_row_3(bitwise_or_8_8_6_z_row_3),
    .z_row_4(bitwise_or_8_8_6_z_row_4), .z_row_5(bitwise_or_8_8_6_z_row_5),
    .z_row_6(bitwise_or_8_8_6_z_row_6), .z_row_7(bitwise_or_8_8_6_z_row_7));
  bitwise_or_8_8 bitwise_or_8_8_7 (
    .x_row_0(bitwise_or_8_8_6_z_row_0), .x_row_1(bitwise_or_8_8_6_z_row_1),
    .x_row_2(bitwise_or_8_8_6_z_row_2), .x_row_3(bitwise_or_8_8_6_z_row_3),
    .x_row_4(bitwise_or_8_8_6_z_row_4), .x_row_5(bitwise_or_8_8_6_z_row_5),
    .x_row_6(bitwise_or_8_8_6_z_row_6), .x_row_7(bitwise_or_8_8_6_z_row_7), .y_row_0(8'h80), .y_row_1(8'h40),
    .y_row_2(8'h20), .y_row_3(8'h10), .y_row_4(8'h8), .y_row_5(8'h4), .y_row_6(8'h2), .y_row_7(8'h1),
    .z_row_0(bitwise_or_8_8_7_z_row_0), .z_row_1(bitwise_or_8_8_7_z_row_1),
    .z_row_2(bitwise_or_8_8_7_z_row_2), .z_row_3(bitwise_or_8_8_7_z_row_3),
    .z_row_4(bitwise_or_8_8_7_z_row_4), .z_row_5(bitwise_or_8_8_7_z_row_5),
    .z_row_6(bitwise_or_8_8_7_z_row_6), .z_row_7(bitwise_or_8_8_7_z_row_7));
  matrix_and_8_8 matrix_and_8_8_1 (
    .x_row_0(bitwise_or_8_8_7_z_row_0), .x_row_1(bitwise_or_8_8_7_z_row_1),
    .x_row_2(bitwise_or_8_8_7_z_row_2), .x_row_3(bitwise_or_8_8_7_z_row_3),
    .x_row_4(bitwise_or_8_8_7_z_row_4), .x_row_5(bitwise_or_8_8_7_z_row_5),
    .x_row_6(bitwise_or_8_8_7_z_row_6), .x_row_7(bitwise_or_8_8_7_z_row_7), .z(is_connected));
endmodule

module matrix_and_8_8 (
  input  [7:0] x_row_0,
  input  [7:0] x_row_1,
  input  [7:0] x_row_2,
  input  [7:0] x_row_3,
  input  [7:0] x_row_4,
  input  [7:0] x_row_5,
  input  [7:0] x_row_6,
  input  [7:0] x_row_7,
  output z
);

  wire and_1_out, and_2_out, and_3_out, and_4_out, and_5_out, and_6_out, and_7_out, and_8_out, and_9_out,
       and_10_out, and_11_out, and_12_out, and_13_out, and_14_out, and_15_out, and_16_out, and_17_out,
       and_18_out, and_19_out, and_20_out, and_21_out, and_22_out, and_23_out, and_24_out, and_25_out,
       and_26_out, and_27_out, and_28_out, and_29_out, and_30_out, and_31_out, and_32_out, and_33_out,
       and_34_out, and_35_out, and_36_out, and_37_out, and_38_out, and_39_out, and_40_out, and_41_out,
       and_42_out, and_43_out, and_44_out, and_45_out, and_46_out, and_47_out, and_48_out, and_49_out,
       and_50_out, and_51_out, and_52_out, and_53_out, and_54_out, and_55_out, and_56_out, and_57_out,
       and_58_out, and_59_out, and_60_out, and_61_out, and_62_out;

  and and_1 (and_1_out, x_row_0[0], x_row_0[1]);
  and and_2 (and_2_out, x_row_0[2], x_row_0[3]);
  and and_3 (and_3_out, x_row_0[4], x_row_0[5]);
  and and_4 (and_4_out, x_row_0[6], x_row_0[7]);
  and and_5 (and_5_out, x_row_1[0], x_row_1[1]);
  and and_6 (and_6_out, x_row_1[2], x_row_1[3]);
  and and_7 (and_7_out, x_row_1[4], x_row_1[5]);
  and and_8 (and_8_out, x_row_1[6], x_row_1[7]);
  and and_9 (and_9_out, x_row_2[0], x_row_2[1]);
  and and_10 (and_10_out, x_row_2[2], x_row_2[3]);
  and and_11 (and_11_out, x_row_2[4], x_row_2[5]);
  and and_12 (and_12_out, x_row_2[6], x_row_2[7]);
  and and_13 (and_13_out, x_row_3[0], x_row_3[1]);
  and and_14 (and_14_out, x_row_3[2], x_row_3[3]);
  and and_15 (and_15_out, x_row_3[4], x_row_3[5]);
  and and_16 (and_16_out, x_row_3[6], x_row_3[7]);
  and and_17 (and_17_out, x_row_4[0], x_row_4[1]);
  and and_18 (and_18_out, x_row_4[2], x_row_4[3]);
  and and_19 (and_19_out, x_row_4[4], x_row_4[5]);
  and and_20 (and_20_out, x_row_4[6], x_row_4[7]);
  and and_21 (and_21_out, x_row_5[0], x_row_5[1]);
  and and_22 (and_22_out, x_row_5[2], x_row_5[3]);
  and and_23 (and_23_out, x_row_5[4], x_row_5[5]);
  and and_24 (and_24_out, x_row_5[6], x_row_5[7]);
  and and_25 (and_25_out, x_row_6[0], x_row_6[1]);
  and and_26 (and_26_out, x_row_6[2], x_row_6[3]);
  and and_27 (and_27_out, x_row_6[4], x_row_6[5]);
  and and_28 (and_28_out, x_row_6[6], x_row_6[7]);
  and and_29 (and_29_out, x_row_7[0], x_row_7[1]);
  and and_30 (and_30_out, x_row_7[2], x_row_7[3]);
  and and_31 (and_31_out, x_row_7[4], x_row_7[5]);
  and and_32 (and_32_out, x_row_7[6], x_row_7[7]);
  DotMatrix #(.inputtype("row"), .matrixcols(8), .matrixrows(8)) dotmatrix_1 (
    .row0(x_row_0), .row1(x_row_1), .row2(x_row_2), .row3(x_row_3), .row4(x_row_4), .row5(x_row_5),
    .row6(x_row_6), .row7(x_row_7));
  and and_33 (and_33_out, and_1_out, and_2_out);
  and and_34 (and_34_out, and_3_out, and_4_out);
  and and_35 (and_35_out, and_5_out, and_6_out);
  and and_36 (and_36_out, and_7_out, and_8_out);
  and and_37 (and_37_out, and_9_out, and_10_out);
  and and_38 (and_38_out, and_11_out, and_12_out);
  and and_39 (and_39_out, and_13_out, and_14_out);
  and and_40 (and_40_out, and_15_out, and_16_out);
  and and_41 (and_41_out, and_17_out, and_18_out);
  and and_42 (and_42_out, and_19_out, and_20_out);
  and and_43 (and_43_out, and_21_out, and_22_out);
  and and_44 (and_44_out, and_23_out, and_24_out);
  and and_45 (and_45_out, and_25_out, and_26_out);
  and and_46 (and_46_out, and_27_out, and_28_out);
  and and_47 (and_47_out, and_29_out, and_30_out);
  and and_48 (and_48_out, and_31_out, and_32_out);
  and and_49 (and_49_out, and_33_out, and_34_out);
  and and_50 (and_50_out, and_35_out, and_36_out);
  and and_51 (and_51_out, and_37_out, and_38_out);
  and and_52 (and_52_out, and_39_out, and_40_out);
  and and_53 (and_53_out, and_41_out, and_42_out);
  and and_54 (and_54_out, and_43_out, and_44_out);
  and and_55 (and_55_out, and_45_out, and_46_out);
  and and_56 (and_56_out, and_47_out, and_48_out);
  and and_57 (and_57_out, and_49_out, and_50_out);
  and and_58 (and_58_out, and_51_out, and_52_out);
  and and_59 (and_59_out, and_53_out, and_54_out);
  and and_60 (and_60_out, and_55_out, and_56_out);
  and and_61 (and_61_out, and_59_out, and_60_out);
  and and_62 (and_62_out, and_57_out, and_58_out);
  and and_63 (z, and_62_out, and_61_out);

  // Other names for the same wires on the sheet: x00 = x_row_0[0]; x01 = x_row_0[1]; x02 = x_row_0[2];
  //   x03 = x_row_0[3]; x04 = x_row_0[4]; x05 = x_row_0[5]; x06 = x_row_0[6]; x07 = x_row_0[7]; x10 = x_row_1[0];
  //   x11 = x_row_1[1]; x12 = x_row_1[2]; x13 = x_row_1[3]; x14 = x_row_1[4]; x15 = x_row_1[5]; x16 = x_row_1[6];
  //   x17 = x_row_1[7]; x20 = x_row_2[0]; x21 = x_row_2[1]; x22 = x_row_2[2]; x23 = x_row_2[3]; x24 = x_row_2[4];
  //   x25 = x_row_2[5]; x26 = x_row_2[6]; x27 = x_row_2[7]; x30 = x_row_3[0]; x31 = x_row_3[1]; x32 = x_row_3[2];
  //   x33 = x_row_3[3]; x34 = x_row_3[4]; x35 = x_row_3[5]; x36 = x_row_3[6]; x37 = x_row_3[7]; x40 = x_row_4[0];
  //   x41 = x_row_4[1]; x42 = x_row_4[2]; x43 = x_row_4[3]; x44 = x_row_4[4]; x45 = x_row_4[5]; x46 = x_row_4[6];
  //   x47 = x_row_4[7]; x50 = x_row_5[0]; x51 = x_row_5[1]; x52 = x_row_5[2]; x53 = x_row_5[3]; x54 = x_row_5[4];
  //   x55 = x_row_5[5]; x56 = x_row_5[6]; x57 = x_row_5[7]; x60 = x_row_6[0]; x61 = x_row_6[1]; x62 = x_row_6[2];
  //   x63 = x_row_6[3]; x64 = x_row_6[4]; x65 = x_row_6[5]; x66 = x_row_6[6]; x67 = x_row_6[7]; x70 = x_row_7[0];
  //   x71 = x_row_7[1]; x72 = x_row_7[2]; x73 = x_row_7[3]; x74 = x_row_7[4]; x75 = x_row_7[5]; x76 = x_row_7[6];
  //   x77 = x_row_7[7]
endmodule

module is_fully_connected (
  input  [7:0] x_row_0,
  input  [7:0] x_row_1,
  input  [7:0] x_row_2,
  input  [7:0] x_row_3,
  input  [7:0] x_row_4,
  input  [7:0] x_row_5,
  input  [7:0] x_row_6,
  input  [7:0] x_row_7,
  output is_fully_connected
);

  wire [7:0] bitwise_or_8_8_1_z_row_0, bitwise_or_8_8_1_z_row_1, bitwise_or_8_8_1_z_row_2,
       bitwise_or_8_8_1_z_row_3, bitwise_or_8_8_1_z_row_4, bitwise_or_8_8_1_z_row_5,
       bitwise_or_8_8_1_z_row_6, bitwise_or_8_8_1_z_row_7;

  bitwise_or_8_8 bitwise_or_8_8_1 (
    .x_row_0(x_row_0), .x_row_1(x_row_1), .x_row_2(x_row_2), .x_row_3(x_row_3), .x_row_4(x_row_4),
    .x_row_5(x_row_5), .x_row_6(x_row_6), .x_row_7(x_row_7), .y_row_0(8'h80), .y_row_1(8'h40),
    .y_row_2(8'h20), .y_row_3(8'h10), .y_row_4(8'h8), .y_row_5(8'h4), .y_row_6(8'h2), .y_row_7(8'h1),
    .z_row_0(bitwise_or_8_8_1_z_row_0), .z_row_1(bitwise_or_8_8_1_z_row_1),
    .z_row_2(bitwise_or_8_8_1_z_row_2), .z_row_3(bitwise_or_8_8_1_z_row_3),
    .z_row_4(bitwise_or_8_8_1_z_row_4), .z_row_5(bitwise_or_8_8_1_z_row_5),
    .z_row_6(bitwise_or_8_8_1_z_row_6), .z_row_7(bitwise_or_8_8_1_z_row_7));
  matrix_and_8_8 matrix_and_8_8_1 (
    .x_row_0(bitwise_or_8_8_1_z_row_0), .x_row_1(bitwise_or_8_8_1_z_row_1),
    .x_row_2(bitwise_or_8_8_1_z_row_2), .x_row_3(bitwise_or_8_8_1_z_row_3),
    .x_row_4(bitwise_or_8_8_1_z_row_4), .x_row_5(bitwise_or_8_8_1_z_row_5),
    .x_row_6(bitwise_or_8_8_1_z_row_6), .x_row_7(bitwise_or_8_8_1_z_row_7), .z(is_fully_connected));
  DotMatrix #(.inputtype("row"), .matrixcols(8), .matrixrows(8)) dotmatrix_1 (
    .row0(x_row_0), .row1(x_row_1), .row2(x_row_2), .row3(x_row_3), .row4(x_row_4), .row5(x_row_5),
    .row6(x_row_6), .row7(x_row_7));
endmodule

module exactly (
  input  [7:0] x_row_0,
  input  [7:0] x_row_1,
  input  [7:0] x_row_2,
  input  [7:0] x_row_3,
  input  [7:0] x_row_4,
  input  [7:0] x_row_5,
  input  [7:0] x_row_6,
  input  [7:0] x_row_7,
  input  [2:0] from,
  input  [2:0] to,
  input  [2:0] num_steps,
  output path_exists
);

  wire and_2_out, ans0, ans1, ans2, ans3, ans4, ans5, ans6, loop, xnor_1_out, xnor_2_out, xnor_3_out;
  wire [7:0] row0, row1, row2, row3, row4, row5, row6, x1_row_0, x1_row_1, x1_row_2, x1_row_3, x1_row_4,
       x1_row_5, x1_row_6, x1_row_7, x2_row_0, x2_row_1, x2_row_2, x2_row_3, x2_row_4, x2_row_5, x2_row_6,
       x2_row_7, x3_row_0, x3_row_1, x3_row_2, x3_row_3, x3_row_4, x3_row_5, x3_row_6, x3_row_7, x4_row_0,
       x4_row_1, x4_row_2, x4_row_3, x4_row_4, x4_row_5, x4_row_6, x4_row_7, x5_row_0, x5_row_1, x5_row_2,
       x5_row_3, x5_row_4, x5_row_5, x5_row_6, x5_row_7, x6_row_0, x6_row_1, x6_row_2, x6_row_3, x6_row_4,
       x6_row_5, x6_row_6, x6_row_7;

  matmul matmul_1 (
    .x_row_0(x_row_0), .x_row_1(x_row_1), .x_row_2(x_row_2), .x_row_3(x_row_3), .x_row_4(x_row_4),
    .x_row_5(x_row_5), .x_row_6(x_row_6), .x_row_7(x_row_7), .y_row_0(x_row_0), .y_row_1(x_row_1),
    .y_row_2(x_row_2), .y_row_3(x_row_3), .y_row_4(x_row_4), .y_row_5(x_row_5), .y_row_6(x_row_6),
    .y_row_7(x_row_7), .z_row_0(x1_row_0), .z_row_1(x1_row_1), .z_row_2(x1_row_2), .z_row_3(x1_row_3),
    .z_row_4(x1_row_4), .z_row_5(x1_row_5), .z_row_6(x1_row_6), .z_row_7(x1_row_7));
  matmul matmul_2 (
    .x_row_0(x1_row_0), .x_row_1(x1_row_1), .x_row_2(x1_row_2), .x_row_3(x1_row_3), .x_row_4(x1_row_4),
    .x_row_5(x1_row_5), .x_row_6(x1_row_6), .x_row_7(x1_row_7), .y_row_0(x_row_0), .y_row_1(x_row_1),
    .y_row_2(x_row_2), .y_row_3(x_row_3), .y_row_4(x_row_4), .y_row_5(x_row_5), .y_row_6(x_row_6),
    .y_row_7(x_row_7), .z_row_0(x2_row_0), .z_row_1(x2_row_1), .z_row_2(x2_row_2), .z_row_3(x2_row_3),
    .z_row_4(x2_row_4), .z_row_5(x2_row_5), .z_row_6(x2_row_6), .z_row_7(x2_row_7));
  matmul matmul_3 (
    .x_row_0(x2_row_0), .x_row_1(x2_row_1), .x_row_2(x2_row_2), .x_row_3(x2_row_3), .x_row_4(x2_row_4),
    .x_row_5(x2_row_5), .x_row_6(x2_row_6), .x_row_7(x2_row_7), .y_row_0(x_row_0), .y_row_1(x_row_1),
    .y_row_2(x_row_2), .y_row_3(x_row_3), .y_row_4(x_row_4), .y_row_5(x_row_5), .y_row_6(x_row_6),
    .y_row_7(x_row_7), .z_row_0(x3_row_0), .z_row_1(x3_row_1), .z_row_2(x3_row_2), .z_row_3(x3_row_3),
    .z_row_4(x3_row_4), .z_row_5(x3_row_5), .z_row_6(x3_row_6), .z_row_7(x3_row_7));
  matmul matmul_4 (
    .x_row_0(x3_row_0), .x_row_1(x3_row_1), .x_row_2(x3_row_2), .x_row_3(x3_row_3), .x_row_4(x3_row_4),
    .x_row_5(x3_row_5), .x_row_6(x3_row_6), .x_row_7(x3_row_7), .y_row_0(x_row_0), .y_row_1(x_row_1),
    .y_row_2(x_row_2), .y_row_3(x_row_3), .y_row_4(x_row_4), .y_row_5(x_row_5), .y_row_6(x_row_6),
    .y_row_7(x_row_7), .z_row_0(x4_row_0), .z_row_1(x4_row_1), .z_row_2(x4_row_2), .z_row_3(x4_row_3),
    .z_row_4(x4_row_4), .z_row_5(x4_row_5), .z_row_6(x4_row_6), .z_row_7(x4_row_7));
  matmul matmul_5 (
    .x_row_0(x4_row_0), .x_row_1(x4_row_1), .x_row_2(x4_row_2), .x_row_3(x4_row_3), .x_row_4(x4_row_4),
    .x_row_5(x4_row_5), .x_row_6(x4_row_6), .x_row_7(x4_row_7), .y_row_0(x_row_0), .y_row_1(x_row_1),
    .y_row_2(x_row_2), .y_row_3(x_row_3), .y_row_4(x_row_4), .y_row_5(x_row_5), .y_row_6(x_row_6),
    .y_row_7(x_row_7), .z_row_0(x5_row_0), .z_row_1(x5_row_1), .z_row_2(x5_row_2), .z_row_3(x5_row_3),
    .z_row_4(x5_row_4), .z_row_5(x5_row_5), .z_row_6(x5_row_6), .z_row_7(x5_row_7));
  matmul matmul_6 (
    .x_row_0(x5_row_0), .x_row_1(x5_row_1), .x_row_2(x5_row_2), .x_row_3(x5_row_3), .x_row_4(x5_row_4),
    .x_row_5(x5_row_5), .x_row_6(x5_row_6), .x_row_7(x5_row_7), .y_row_0(x_row_0), .y_row_1(x_row_1),
    .y_row_2(x_row_2), .y_row_3(x_row_3), .y_row_4(x_row_4), .y_row_5(x_row_5), .y_row_6(x_row_6),
    .y_row_7(x_row_7), .z_row_0(x6_row_0), .z_row_1(x6_row_1), .z_row_2(x6_row_2), .z_row_3(x6_row_3),
    .z_row_4(x6_row_4), .z_row_5(x6_row_5), .z_row_6(x6_row_6), .z_row_7(x6_row_7));
  DotMatrix #(.inputtype("row"), .matrixcols(8), .matrixrows(8)) dotmatrix_1 (
    .row0(x_row_0), .row1(x_row_1), .row2(x_row_2), .row3(x_row_3), .row4(x_row_4), .row5(x_row_5),
    .row6(x_row_6), .row7(x_row_7));
  Multiplexer #(.select(3), .width(8), .enable("false")) multiplexer_1 (
    .in0(x1_row_0), .in1(x1_row_1), .in2(x1_row_2), .in3(x1_row_3), .in4(x1_row_4), .in5(x1_row_5),
    .in6(x1_row_6), .in7(x1_row_7), .out(row1), .sel(from));
  Multiplexer #(.select(3), .width(8), .enable("false")) multiplexer_2 (
    .in0(x2_row_0), .in1(x2_row_1), .in2(x2_row_2), .in3(x2_row_3), .in4(x2_row_4), .in5(x2_row_5),
    .in6(x2_row_6), .in7(x2_row_7), .out(row2), .sel(from));
  Multiplexer #(.select(3), .width(8), .enable("false")) multiplexer_3 (
    .in0(x3_row_0), .in1(x3_row_1), .in2(x3_row_2), .in3(x3_row_3), .in4(x3_row_4), .in5(x3_row_5),
    .in6(x3_row_6), .in7(x3_row_7), .out(row3), .sel(from));
  Multiplexer #(.select(3), .width(8), .enable("false")) multiplexer_4 (
    .in0(x4_row_0), .in1(x4_row_1), .in2(x4_row_2), .in3(x4_row_3), .in4(x4_row_4), .in5(x4_row_5),
    .in6(x4_row_6), .in7(x4_row_7), .out(row4), .sel(from));
  Multiplexer #(.select(3), .width(8), .enable("false")) multiplexer_5 (
    .in0(x5_row_0), .in1(x5_row_1), .in2(x5_row_2), .in3(x5_row_3), .in4(x5_row_4), .in5(x5_row_5),
    .in6(x5_row_6), .in7(x5_row_7), .out(row5), .sel(from));
  Multiplexer #(.select(3), .width(8), .enable("false")) multiplexer_6 (
    .in0(x6_row_0), .in1(x6_row_1), .in2(x6_row_2), .in3(x6_row_3), .in4(x6_row_4), .in5(x6_row_5),
    .in6(x6_row_6), .in7(x6_row_7), .out(row6), .sel(from));
  Multiplexer #(.select(3), .enable("false")) multiplexer_7 (
    .in0(loop), .in1(ans0), .in2(ans1), .in3(ans2), .in4(ans3), .in5(ans4), .in6(ans5), .in7(ans6),
    .out(path_exists), .sel(num_steps));
  Multiplexer #(.select(3), .enable("false")) multiplexer_8 (
    .in0(row1[7]), .in1(row1[6]), .in2(row1[5]), .in3(row1[4]), .in4(row1[3]), .in5(row1[2]), .in6(row1[1]),
    .in7(row1[0]), .out(ans1), .sel(to));
  Multiplexer #(.select(3), .enable("false")) multiplexer_9 (
    .in0(row2[7]), .in1(row2[6]), .in2(row2[5]), .in3(row2[4]), .in4(row2[3]), .in5(row2[2]), .in6(row2[1]),
    .in7(row2[0]), .out(ans2), .sel(to));
  Multiplexer #(.select(3), .enable("false")) multiplexer_10 (
    .in0(row3[7]), .in1(row3[6]), .in2(row3[5]), .in3(row3[4]), .in4(row3[3]), .in5(row3[2]), .in6(row3[1]),
    .in7(row3[0]), .out(ans3), .sel(to));
  Multiplexer #(.select(3), .enable("false")) multiplexer_11 (
    .in0(row4[7]), .in1(row4[6]), .in2(row4[5]), .in3(row4[4]), .in4(row4[3]), .in5(row4[2]), .in6(row4[1]),
    .in7(row4[0]), .out(ans4), .sel(to));
  Multiplexer #(.select(3), .enable("false")) multiplexer_12 (
    .in0(row5[7]), .in1(row5[6]), .in2(row5[5]), .in3(row5[4]), .in4(row5[3]), .in5(row5[2]), .in6(row5[1]),
    .in7(row5[0]), .out(ans5), .sel(to));
  Multiplexer #(.select(3), .enable("false")) multiplexer_13 (
    .in0(row6[7]), .in1(row6[6]), .in2(row6[5]), .in3(row6[4]), .in4(row6[3]), .in5(row6[2]), .in6(row6[1]),
    .in7(row6[0]), .out(ans6), .sel(to));
  Multiplexer #(.select(3), .width(8), .enable("false")) multiplexer_14 (
    .in0(x_row_0), .in1(x_row_1), .in2(x_row_2), .in3(x_row_3), .in4(x_row_4), .in5(x_row_5), .in6(x_row_6),
    .in7(x_row_7), .out(row0), .sel(from));
  Multiplexer #(.select(3), .enable("false")) multiplexer_15 (
    .in0(row0[7]), .in1(row0[6]), .in2(row0[5]), .in3(row0[4]), .in4(row0[3]), .in5(row0[2]), .in6(row0[1]),
    .in7(row0[0]), .out(ans0), .sel(to));
  and and_1 (loop, and_2_out, xnor_3_out);
  and and_2 (and_2_out, xnor_1_out, xnor_2_out);
  xnor xnor_1 (xnor_1_out, from[0], to[0]);
  xnor xnor_2 (xnor_2_out, from[1], to[1]);
  xnor xnor_3 (xnor_3_out, from[2], to[2]);
endmodule

module atmost (
  input  [7:0] x_row_0,
  input  [7:0] x_row_1,
  input  [7:0] x_row_2,
  input  [7:0] x_row_3,
  input  [7:0] x_row_4,
  input  [7:0] x_row_5,
  input  [7:0] x_row_6,
  input  [7:0] x_row_7,
  input  [2:0] from,
  input  [2:0] to,
  input  [2:0] num_steps,
  output path_exists
);

  wire and_2_out, and_3_out, and_4_out, and_5_out, and_6_out, and_7_out, and_8_out, and_9_out, and_10_out,
       and_11_out, and_12_out, and_13_out, and_14_out, and_15_out, and_16_out, ans0, ans1, ans2, ans3, ans4,
       ans5, ans6, loop, or_1_out, or_2_out, or_3_out, or_4_out, or_5_out, or_6_out, or_7_out, or_8_out,
       or_9_out, or_10_out, or_11_out, xnor_1_out, xnor_2_out, xnor_3_out;
  wire [7:0] row0, row1, row2, row3, row4, row5, row6, x1_row_0, x1_row_1, x1_row_2, x1_row_3, x1_row_4,
       x1_row_5, x1_row_6, x1_row_7, x2_row_0, x2_row_1, x2_row_2, x2_row_3, x2_row_4, x2_row_5, x2_row_6,
       x2_row_7, x3_row_0, x3_row_1, x3_row_2, x3_row_3, x3_row_4, x3_row_5, x3_row_6, x3_row_7, x4_row_0,
       x4_row_1, x4_row_2, x4_row_3, x4_row_4, x4_row_5, x4_row_6, x4_row_7, x5_row_0, x5_row_1, x5_row_2,
       x5_row_3, x5_row_4, x5_row_5, x5_row_6, x5_row_7, x6_row_0, x6_row_1, x6_row_2, x6_row_3, x6_row_4,
       x6_row_5, x6_row_6, x6_row_7;

  matmul matmul_1 (
    .x_row_0(x_row_0), .x_row_1(x_row_1), .x_row_2(x_row_2), .x_row_3(x_row_3), .x_row_4(x_row_4),
    .x_row_5(x_row_5), .x_row_6(x_row_6), .x_row_7(x_row_7), .y_row_0(x_row_0), .y_row_1(x_row_1),
    .y_row_2(x_row_2), .y_row_3(x_row_3), .y_row_4(x_row_4), .y_row_5(x_row_5), .y_row_6(x_row_6),
    .y_row_7(x_row_7), .z_row_0(x1_row_0), .z_row_1(x1_row_1), .z_row_2(x1_row_2), .z_row_3(x1_row_3),
    .z_row_4(x1_row_4), .z_row_5(x1_row_5), .z_row_6(x1_row_6), .z_row_7(x1_row_7));
  matmul matmul_2 (
    .x_row_0(x1_row_0), .x_row_1(x1_row_1), .x_row_2(x1_row_2), .x_row_3(x1_row_3), .x_row_4(x1_row_4),
    .x_row_5(x1_row_5), .x_row_6(x1_row_6), .x_row_7(x1_row_7), .y_row_0(x_row_0), .y_row_1(x_row_1),
    .y_row_2(x_row_2), .y_row_3(x_row_3), .y_row_4(x_row_4), .y_row_5(x_row_5), .y_row_6(x_row_6),
    .y_row_7(x_row_7), .z_row_0(x2_row_0), .z_row_1(x2_row_1), .z_row_2(x2_row_2), .z_row_3(x2_row_3),
    .z_row_4(x2_row_4), .z_row_5(x2_row_5), .z_row_6(x2_row_6), .z_row_7(x2_row_7));
  matmul matmul_3 (
    .x_row_0(x2_row_0), .x_row_1(x2_row_1), .x_row_2(x2_row_2), .x_row_3(x2_row_3), .x_row_4(x2_row_4),
    .x_row_5(x2_row_5), .x_row_6(x2_row_6), .x_row_7(x2_row_7), .y_row_0(x_row_0), .y_row_1(x_row_1),
    .y_row_2(x_row_2), .y_row_3(x_row_3), .y_row_4(x_row_4), .y_row_5(x_row_5), .y_row_6(x_row_6),
    .y_row_7(x_row_7), .z_row_0(x3_row_0), .z_row_1(x3_row_1), .z_row_2(x3_row_2), .z_row_3(x3_row_3),
    .z_row_4(x3_row_4), .z_row_5(x3_row_5), .z_row_6(x3_row_6), .z_row_7(x3_row_7));
  matmul matmul_4 (
    .x_row_0(x3_row_0), .x_row_1(x3_row_1), .x_row_2(x3_row_2), .x_row_3(x3_row_3), .x_row_4(x3_row_4),
    .x_row_5(x3_row_5), .x_row_6(x3_row_6), .x_row_7(x3_row_7), .y_row_0(x_row_0), .y_row_1(x_row_1),
    .y_row_2(x_row_2), .y_row_3(x_row_3), .y_row_4(x_row_4), .y_row_5(x_row_5), .y_row_6(x_row_6),
    .y_row_7(x_row_7), .z_row_0(x4_row_0), .z_row_1(x4_row_1), .z_row_2(x4_row_2), .z_row_3(x4_row_3),
    .z_row_4(x4_row_4), .z_row_5(x4_row_5), .z_row_6(x4_row_6), .z_row_7(x4_row_7));
  matmul matmul_5 (
    .x_row_0(x4_row_0), .x_row_1(x4_row_1), .x_row_2(x4_row_2), .x_row_3(x4_row_3), .x_row_4(x4_row_4),
    .x_row_5(x4_row_5), .x_row_6(x4_row_6), .x_row_7(x4_row_7), .y_row_0(x_row_0), .y_row_1(x_row_1),
    .y_row_2(x_row_2), .y_row_3(x_row_3), .y_row_4(x_row_4), .y_row_5(x_row_5), .y_row_6(x_row_6),
    .y_row_7(x_row_7), .z_row_0(x5_row_0), .z_row_1(x5_row_1), .z_row_2(x5_row_2), .z_row_3(x5_row_3),
    .z_row_4(x5_row_4), .z_row_5(x5_row_5), .z_row_6(x5_row_6), .z_row_7(x5_row_7));
  matmul matmul_6 (
    .x_row_0(x5_row_0), .x_row_1(x5_row_1), .x_row_2(x5_row_2), .x_row_3(x5_row_3), .x_row_4(x5_row_4),
    .x_row_5(x5_row_5), .x_row_6(x5_row_6), .x_row_7(x5_row_7), .y_row_0(x_row_0), .y_row_1(x_row_1),
    .y_row_2(x_row_2), .y_row_3(x_row_3), .y_row_4(x_row_4), .y_row_5(x_row_5), .y_row_6(x_row_6),
    .y_row_7(x_row_7), .z_row_0(x6_row_0), .z_row_1(x6_row_1), .z_row_2(x6_row_2), .z_row_3(x6_row_3),
    .z_row_4(x6_row_4), .z_row_5(x6_row_5), .z_row_6(x6_row_6), .z_row_7(x6_row_7));
  DotMatrix #(.inputtype("row"), .matrixcols(8), .matrixrows(8)) dotmatrix_1 (
    .row0(x_row_0), .row1(x_row_1), .row2(x_row_2), .row3(x_row_3), .row4(x_row_4), .row5(x_row_5),
    .row6(x_row_6), .row7(x_row_7));
  Multiplexer #(.select(3), .width(8), .enable("false")) multiplexer_1 (
    .in0(x1_row_0), .in1(x1_row_1), .in2(x1_row_2), .in3(x1_row_3), .in4(x1_row_4), .in5(x1_row_5),
    .in6(x1_row_6), .in7(x1_row_7), .out(row1), .sel(from));
  Multiplexer #(.select(3), .width(8), .enable("false")) multiplexer_2 (
    .in0(x2_row_0), .in1(x2_row_1), .in2(x2_row_2), .in3(x2_row_3), .in4(x2_row_4), .in5(x2_row_5),
    .in6(x2_row_6), .in7(x2_row_7), .out(row2), .sel(from));
  Multiplexer #(.select(3), .width(8), .enable("false")) multiplexer_3 (
    .in0(x3_row_0), .in1(x3_row_1), .in2(x3_row_2), .in3(x3_row_3), .in4(x3_row_4), .in5(x3_row_5),
    .in6(x3_row_6), .in7(x3_row_7), .out(row3), .sel(from));
  Multiplexer #(.select(3), .width(8), .enable("false")) multiplexer_4 (
    .in0(x4_row_0), .in1(x4_row_1), .in2(x4_row_2), .in3(x4_row_3), .in4(x4_row_4), .in5(x4_row_5),
    .in6(x4_row_6), .in7(x4_row_7), .out(row4), .sel(from));
  Multiplexer #(.select(3), .width(8), .enable("false")) multiplexer_5 (
    .in0(x5_row_0), .in1(x5_row_1), .in2(x5_row_2), .in3(x5_row_3), .in4(x5_row_4), .in5(x5_row_5),
    .in6(x5_row_6), .in7(x5_row_7), .out(row5), .sel(from));
  Multiplexer #(.select(3), .width(8), .enable("false")) multiplexer_6 (
    .in0(x6_row_0), .in1(x6_row_1), .in2(x6_row_2), .in3(x6_row_3), .in4(x6_row_4), .in5(x6_row_5),
    .in6(x6_row_6), .in7(x6_row_7), .out(row6), .sel(from));
  Multiplexer #(.select(3), .enable("false")) multiplexer_7 (
    .in0(row1[7]), .in1(row1[6]), .in2(row1[5]), .in3(row1[4]), .in4(row1[3]), .in5(row1[2]), .in6(row1[1]),
    .in7(row1[0]), .out(ans1), .sel(to));
  Multiplexer #(.select(3), .enable("false")) multiplexer_8 (
    .in0(row2[7]), .in1(row2[6]), .in2(row2[5]), .in3(row2[4]), .in4(row2[3]), .in5(row2[2]), .in6(row2[1]),
    .in7(row2[0]), .out(ans2), .sel(to));
  Multiplexer #(.select(3), .enable("false")) multiplexer_9 (
    .in0(row3[7]), .in1(row3[6]), .in2(row3[5]), .in3(row3[4]), .in4(row3[3]), .in5(row3[2]), .in6(row3[1]),
    .in7(row3[0]), .out(ans3), .sel(to));
  Multiplexer #(.select(3), .enable("false")) multiplexer_10 (
    .in0(row4[7]), .in1(row4[6]), .in2(row4[5]), .in3(row4[4]), .in4(row4[3]), .in5(row4[2]), .in6(row4[1]),
    .in7(row4[0]), .out(ans4), .sel(to));
  Multiplexer #(.select(3), .enable("false")) multiplexer_11 (
    .in0(row5[7]), .in1(row5[6]), .in2(row5[5]), .in3(row5[4]), .in4(row5[3]), .in5(row5[2]), .in6(row5[1]),
    .in7(row5[0]), .out(ans5), .sel(to));
  Multiplexer #(.select(3), .enable("false")) multiplexer_12 (
    .in0(row6[7]), .in1(row6[6]), .in2(row6[5]), .in3(row6[4]), .in4(row6[3]), .in5(row6[2]), .in6(row6[1]),
    .in7(row6[0]), .out(ans6), .sel(to));
  Multiplexer #(.select(3), .width(8), .enable("false")) multiplexer_13 (
    .in0(x_row_0), .in1(x_row_1), .in2(x_row_2), .in3(x_row_3), .in4(x_row_4), .in5(x_row_5), .in6(x_row_6),
    .in7(x_row_7), .out(row0), .sel(from));
  Multiplexer #(.select(3), .enable("false")) multiplexer_14 (
    .in0(row0[7]), .in1(row0[6]), .in2(row0[5]), .in3(row0[4]), .in4(row0[3]), .in5(row0[2]), .in6(row0[1]),
    .in7(row0[0]), .out(ans0), .sel(to));
  and and_1 (loop, and_2_out, and_3_out);
  and and_2 (and_2_out, xnor_1_out, xnor_2_out);
  and and_3 (and_3_out, xnor_2_out, xnor_3_out);
  xnor xnor_1 (xnor_1_out, from[0], to[0]);
  xnor xnor_2 (xnor_2_out, from[1], to[1]);
  xnor xnor_3 (xnor_3_out, from[2], to[2]);
  and and_4 (and_4_out, num_steps[1], num_steps[2]);
  and and_5 (and_5_out, num_steps[2], num_steps[1]);
  and and_6 (and_6_out, num_steps[2], num_steps[1]);
  and and_7 (and_7_out, num_steps[2], num_steps[0]);
  and and_8 (and_8_out, num_steps[0], num_steps[1]);
  or or_1 (or_1_out, num_steps[2], num_steps[1]);
  and and_9 (and_9_out, and_4_out, num_steps[0]);
  and and_10 (and_10_out, and_5_out, ans5);
  or or_2 (or_2_out, and_6_out, and_7_out);
  or or_3 (or_3_out, and_8_out, num_steps[2]);
  or or_4 (or_4_out, num_steps[2], num_steps[1]);
  and and_11 (and_11_out, and_9_out, ans6);
  and and_12 (and_12_out, ans2, or_3_out);
  or or_5 (or_5_out, num_steps[0], or_1_out);
  and and_13 (and_13_out, or_4_out, ans1);
  and and_14 (and_14_out, num_steps[2], ans3);
  and and_15 (and_15_out, or_2_out, ans4);
  and and_16 (and_16_out, ans0, or_5_out);
  or or_6 (or_6_out, and_11_out, and_10_out);
  or or_7 (or_7_out, and_15_out, and_12_out);
  or or_8 (or_8_out, and_13_out, and_14_out);
  or or_9 (or_9_out, and_16_out, loop);
  or or_10 (or_10_out, or_6_out, or_7_out);
  or or_11 (or_11_out, or_9_out, or_8_out);
  or or_12 (path_exists, or_10_out, or_11_out);

  // Other names for the same wires on the sheet: ns_0 = num_steps[0]; ns_1 = num_steps[1]; ns_2 = num_steps[2]
endmodule
