// Logisim project 209127612_recursion.circ as structural Verilog: 26 circuits, main circuit matmul
module matmul (
  input  [7:0] x_row_0,
  input  [7:0] x_row_1,
  input  [7:0] x_row_2,
  input  [7:0] x_row_3,
  input  [7:0] x_row_4,
  input  [7:0] x_row_5,
  input  [7:0] x_row_6,
  input  [7:0] x_row_7,
  input  [7:0] y_row_0,
  input  [7:0] y_row_1,
  input  [7:0] y_row_2,
  input  [7:0] y_row_3,
  input  [7:0] y_row_4,
  input  [7:0] y_row_5,
  input  [7:0] y_row_6,
  input  [7:0] y_row_7,
  output [7:0] z_row_0,
  output [7:0] z_row_1,
  output [7:0] z_row_2,
  output [7:0] z_row_3,
  output [7:0] z_row_4,
  output [7:0] z_row_5,
  output [7:0] z_row_6,
  output [7:0] z_row_7
);

  wire [7:0] y_col_0, y_col_1, y_col_2, y_col_3, y_col_4, y_col_5, y_col_6, y_col_7;

  matmul_step_2 matmul_step_2_1 (
    .row(x_row_0), .col_0(y_col_0), .col_1(y_col_1), .col_2(y_col_2), .col_3(y_col_3), .col_4(y_col_4),
    .col_5(y_col_5), .col_6(y_col_6), .col_7(y_col_7), .product_row(z_row_0));
  matmul_step_2 matmul_step_2_2 (
    .row(x_row_1), .col_0(y_col_0), .col_1(y_col_1), .col_2(y_col_2), .col_3(y_col_3), .col_4(y_col_4),
    .col_5(y_col_5), .col_6(y_col_6), .col_7(y_col_7), .product_row(z_row_1));
  matmul_step_2 matmul_step_2_3 (
    .row(x_row_6), .col_0(y_col_0), .col_1(y_col_1), .col_2(y_col_2), .col_3(y_col_3), .col_4(y_col_4),
    .col_5(y_col_5), .col_6(y_col_6), .col_7(y_col_7), .product_row(z_row_6));
  DotMatrix #(.inputtype("row"), .matrixcols(8), .matrixrows(8)) dotmatrix_1 (
    .row0(x_row_0), .row1(x_row_1), .row2(x_row_2), .row3(x_row_3), .row4(x_row_4), .row5(x_row_5),
    .row6(x_row_6), .row7(x_row_7));
  DotMatrix #(.inputtype("row"), .matrixcols(8), .matrixrows(8)) dotmatrix_2 (
    .row0(y_row_0), .row1(y_row_1), .row2(y_row_2), .row3(y_row_3), .row4(y_row_4), .row5(y_row_5),
    .row6(y_row_6), .row7(y_row_7));
  transpose transpose_1 (
    .row_0(y_row_0), .row_1(y_row_1), .row_2(y_row_2), .row_3(y_row_3), .row_4(y_row_4), .row_5(y_row_5),
    .row_6(y_row_6), .row_7(y_row_7), .column_0(y_col_0), .column_1(y_col_1), .column_2(y_col_2),
    .column_3(y_col_3), .column_4(y_col_4), .column_5(y_col_5), .column_6(y_col_6), .column_7(y_col_7));
  matmul_step_2 matmul_step_2_4 (
    .row(x_row_2), .col_0(y_col_0), .col_1(y_col_1), .col_2(y_col_2), .col_3(y_col_3), .col_4(y_col_4),
    .col_5(y_col_5), .col_6(y_col_6), .col_7(y_col_7), .product_row(z_row_2));
  matmul_step_2 matmul_step_2_5 (
    .row(x_row_3), .col_0(y_col_0), .col_1(y_col_1), .col_2(y_col_2), .col_3(y_col_3), .col_4(y_col_4),
    .col_5(y_col_5), .col_6(y_col_6), .col_7(y_col_7), .product_row(z_row_3));
  matmul_step_2 matmul_step_2_6 (
    .row(x_row_7), .col_0(y_col_0), .col_1(y_col_1), .col_2(y_col_2), .col_3(y_col_3), .col_4(y_col_4),
    .col_5(y_col_5), .col_6(y_col_6), .col_7(y_col_7), .product_row(z_row_7));
  DotMatrix #(.inputtype("row"), .matrixcols(8), .matrixrows(8)) dotmatrix_3 (
    .row0(z_row_0), .row1(z_row_1), .row2(z_row_2), .row3(z_row_3), .row4(z_row_4), .row5(z_row_5),
    .row6(z_row_6), .row7(z_row_7));
  matmul_step_2 matmul_step_2_7 (
    .row(x_row_4), .col_0(y_col_0), .col_1(y_col_1), .col_2(y_col_2), .col_3(y_col_3), .col_4(y_col_4),
    .col_5(y_col_5), .col_6(y_col_6), .col_7(y_col_7), .product_row(z_row_4));
  matmul_step_2 matmul_step_2_8 (
    .row(x_row_5), .col_0(y_col_0), .col_1(y_col_1), .col_2(y_col_2), .col_3(y_col_3), .col_4(y_col_4),
    .col_5(y_col_5), .col_6(y_col_6), .col_7(y_col_7), .product_row(z_row_5));
endmodule

module transpose (
  input  [7:0] row_0,
  input  [7:0] row_1,
  input  [7:0] row_2,
  input  [7:0] row_3,
  input  [7:0] row_4,
  input  [7:0] row_5,
  input  [7:0] row_6,
  input  [7:0] row_7,
  output [7:0] column_0,
  output [7:0] column_1,
  output [7:0] column_2,
  output [7:0] column_3,
  output [7:0] column_4,
  output [7:0] column_5,
  output [7:0] column_6,
  output [7:0] column_7
);

  extract_col extract_col_1 (
    .in_1(3'b000), .row_0(row_0), .row_1(row_1), .row_2(row_2), .row_3(row_3), .row_4(row_4), .row_5(row_5),
    .row_6(row_6), .row_7(row_7), .b(column_0));
  extract_col extract_col_2 (
    .in_1(3'b100), .row_0(row_0), .row_1(row_1), .row_2(row_2), .row_3(row_3), .row_4(row_4), .row_5(row_5),
    .row_6(row_6), .row_7(row_7), .b(column_4));
  extract_col extract_col_3 (
    .in_1(3'b001), .row_0(row_0), .row_1(row_1), .row_2(row_2), .row_3(row_3), .row_4(row_4), .row_5(row_5),
    .row_6(row_6), .row_7(row_7), .b(column_1));
  extract_col extract_col_4 (
    .in_1(3'b101), .row_0(row_0), .row_1(row_1), .row_2(row_2), .row_3(row_3), .row_4(row_4), .row_5(row_5),
    .row_6(row_6), .row_7(row_7), .b(column_5));
  extract_col extract_col_5 (
    .in_1(3'b010), .row_0(row_0), .row_1(row_1), .row_2(row_2), .row_3(row_3), .row_4(row_4), .row_5(row_5),
    .row_6(row_6), .row_7(row_7), .b(column_2));
  extract_col extract_col_6 (
    .in_1(3'b110), .row_0(row_0), .row_1(row_1), .row_2(row_2), .row_3(row_3), .row_4(row_4), .row_5(row_5),
    .row_6(row_6), .row_7(row_7), .b(column_6));
  extract_col extract_col_7 (
    .in_1(3'b011), .row_0(row_0), .row_1(row_1), .row_2(row_2), .row_3(row_3), .row_4(row_4), .row_5(row_5),
    .row_6(row_6), .row_7(row_7), .b(column_3));
  extract_col extract_col_8 (
    .in_1(3'b111), .row_0(row_0), .row_1(row_1), .row_2(row_2), .row_3(row_3), .row_4(row_4), .row_5(row_5),
    .row_6(row_6), .row_7(row_7), .b(column_7));
endmodule

module extract_col (
  input  [2:0] in_1,
  input  [7:0] row_0,
  input  [7:0] row_1,
  input  [7:0] row_2,
  input  [7:0] row_3,
  input  [7:0] row_4,
  input  [7:0] row_5,
  input  [7:0] row_6,
  input  [7:0] row_7,
  output [7:0] b
);

  wire [2:0] not_1_out, not_2_out, not_3_out, not_4_out, not_5_out, not_6_out, not_7_out, not_8_out;

  BitSelector bitselector_1 (.in(row_0), .out(b[7]), .sel(not_1_out));
  assign not_1_out = ~in_1;  // NOT_Gate not_1, 3 bits wide
  BitSelector bitselector_2 (.in(row_1), .out(b[6]), .sel(not_2_out));
  assign not_2_out = ~in_1;  // NOT_Gate not_2, 3 bits wide
  BitSelector bitselector_3 (.in(row_2), .out(b[5]), .sel(not_3_out));
  assign not_3_out = ~in_1;  // NOT_Gate not_3, 3 bits wide
  BitSelector bitselector_4 (.in(row_3), .out(b[4]), .sel(not_4_out));
  assign not_4_out = ~in_1;  // NOT_Gate not_4, 3 bits wide
  BitSelector bitselector_5 (.in(row_4), .out(b[3]), .sel(not_5_out));
  assign not_5_out = ~in_1;  // NOT_Gate not_5, 3 bits wide
  BitSelector bitselector_6 (.in(row_5), .out(b[2]), .sel(not_6_out));
  assign not_6_out = ~in_1;  // NOT_Gate not_6, 3 bits wide
  BitSelector bitselector_7 (.in(row_6), .out(b[1]), .sel(not_7_out));
  assign not_7_out = ~in_1;  // NOT_Gate not_7, 3 bits wide
  BitSelector bitselector_8 (.in(row_7), .out(b[0]), .sel(not_8_out));
  assign not_8_out = ~in_1;  // NOT_Gate not_8, 3 bits wide

  // Other names for the same wires on the sheet: col[7:0] = b; col_num[2:0] = in_1
endmodule

module matmul_step_1 (
  input  [7:0] row,
  input  [7:0] col,
  output \output 
);

  wire and_1_out, and_2_out, and_3_out, and_4_out, and_5_out, and_6_out, and_7_out, and_8_out, or_1_out,
       or_2_out, or_3_out, or_4_out, or_5_out, or_6_out;

  and and_1 (and_1_out, row[0], col[0]);
  and and_2 (and_2_out, row[1], col[1]);
  and and_3 (and_3_out, row[2], col[2]);
  and and_4 (and_4_out, row[3], col[3]);
  and and_5 (and_5_out, row[4], col[4]);
  and and_6 (and_6_out, row[5], col[5]);
  and and_7 (and_7_out, row[6], col[6]);
  and and_8 (and_8_out, row[7], col[7]);
  or or_1 (or_1_out, and_1_out, and_2_out);
  or or_2 (or_2_out, and_3_out, and_4_out);
  or or_3 (or_3_out, and_5_out, and_6_out);
  or or_4 (or_4_out, and_7_out, and_8_out);
  or or_5 (or_5_out, or_1_out, or_2_out);
  or or_6 (or_6_out, or_3_out, or_4_out);
  or or_7 (\output , or_5_out, or_6_out);

  // Other names for the same wires on the sheet: y00 = col[0]; y01 = col[1]; y02 = col[2]; y03 = col[3]; y04 = col[4];
  //   y05 = col[5]; y06 = col[6]; y07 = col[7]; x00 = row[0]; x01 = row[1]; x02 = row[2]; x03 = row[3]; x04 = row[4];
  //   x05 = row[5]; x06 = row[6]; x07 = row[7]
endmodule

module matmul_step_2 (
  input  [7:0] row,
  input  [7:0] col_0,
  input  [7:0] col_1,
  input  [7:0] col_2,
  input  [7:0] col_3,
  input  [7:0] col_4,
  input  [7:0] col_5,
  input  [7:0] col_6,
  input  [7:0] col_7,
  output [7:0] product_row
);

  matmul_step_1 matmul_step_1_1 (.row(row), .col(col_7), .\output (product_row[0]));
  matmul_step_1 matmul_step_1_2 (.row(row), .col(col_6), .\output (product_row[1]));
  matmul_step_1 matmul_step_1_3 (.row(row), .col(col_5), .\output (product_row[2]));
  matmul_step_1 matmul_step_1_4 (.row(row), .col(col_4), .\output (product_row[3]));
  matmul_step_1 matmul_step_1_5 (.row(row), .col(col_3), .\output (product_row[4]));
  matmul_step_1 matmul_step_1_6 (.row(row), .col(col_2), .\output (product_row[5]));
  matmul_step_1 matmul_step_1_7 (.row(row), .col(col_1), .\output (product_row[6]));
  matmul_step_1 matmul_step_1_8 (.row(row), .col(col_0), .\output (product_row[7]));
endmodule

module pow_0 (
  input  [7:0] x_row_0,
  input  [7:0] x_row_1,
  input  [7:0] x_row_2,
  input  [7:0] x_row_3,
  input  [7:0] x_row_4,
  input  [7:0] x_row_5,
  input  [7:0] x_row_6,
  input  [7:0] x_row_7,
  output [7:0] z_row_0,
  output [7:0] z_row_1,
  output [7:0] z_row_2,
  output [7:0] z_row_3,
  output [7:0] z_row_4,
  output [7:0] z_row_5,
  output [7:0] z_row_6,
  output [7:0] z_row_7
);

  DotMatrix #(.inputtype("row"), .matrixcols(8), .matrixrows(8)) dotmatrix_1 (
    .row0(x_row_0), .row1(x_row_1), .row2(x_row_2), .row3(x_row_3), .row4(x_row_4), .row5(x_row_5),
    .row6(x_row_6), .row7(x_row_7));
  DotMatrix #(.inputtype("row"), .matrixcols(8), .matrixrows(8)) dotmatrix_2 (
    .row0(8'h80), .row1(8'h40), .row2(8'h20), .row3(8'h10), .row4(8'h8), .row5(8'h4), .row6(8'h2), .row7(8'h1));

  assign z_row_0 = 8'h80;
  assign z_row_1 = 8'h40;
  assign z_row_2 = 8'h20;
  assign z_row_3 = 8'h10;
  assign z_row_4 = 8'h8;
  assign z_row_5 = 8'h4;
  assign z_row_6 = 8'h2;
  assign z_row_7 = 8'h1;
endmodule

module pow_1 (
  input  [7:0] x_row_0,
  input  [7:0] x_row_1,
  input  [7:0] x_row_2,
  input  [7:0] x_row_3,
  input  [7:0] x_row_4,
  input  [7:0] x_row_5,
  input  [7:0] x_row_6,
  input  [7:0] x_row_7,
  output [7:0] z_row_0,
  output [7:0] z_row_1,
  output [7:0] z_row_2,
  output [7:0] z_row_3,
  output [7:0] z_row_4,
  output [7:0] z_row_5,
  output [7:0] z_row_6,
  output [7:0] z_row_7
);

  DotMatrix #(.inputtype("row"), .matrixcols(8), .matrixrows(8)) dotmatrix_1 (
    .row0(x_row_0), .row1(x_row_1), .row2(x_row_2), .row3(x_row_3), .row4(x_row_4), .row5(x_row_5),
    .row6(x_row_6), .row7(x_row_7));
  DotMatrix #(.inputtype("row"), .matrixcols(8), .matrixrows(8)) dotmatrix_2 (
    .row0(x_row_0), .row1(x_row_1), .row2(x_row_2), .row3(x_row_3), .row4(x_row_4), .row5(x_row_5),
    .row6(x_row_6), .row7(x_row_7));

  assign z_row_0 = x_row_0;
  assign z_row_1 = x_row_1;
  assign z_row_2 = x_row_2;
  assign z_row_3 = x_row_3;
  assign z_row_4 = x_row_4;
  assign z_row_5 = x_row_5;
  assign z_row_6 = x_row_6;
  assign z_row_7 = x_row_7;
endmodule

module pow_2 (
  input  [7:0] x_row_0,
  input  [7:0] x_row_1,
  input  [7:0] x_row_2,
  input  [7:0] x_row_3,
  input  [7:0] x_row_4,
  input  [7:0] x_row_5,
  input  [7:0] x_row_6,
  input  [7:0] x_row_7,
  output [7:0] z_row_0,
  output [7:0] z_row_1,
  output [7:0] z_row_2,
  output [7:0] z_row_3,
  output [7:0] z_row_4,
  output [7:0] z_row_5,
  output [7:0] z_row_6,
  output [7:0] z_row_7
);

  DotMatrix #(.inputtype("row"), .matrixcols(8), .matrixrows(8)) dotmatrix_1 (
    .row0(x_row_0), .row1(x_row_1), .row2(x_row_2), .row3(x_row_3), .row4(x_row_4), .row5(x_row_5),
    .row6(x_row_6), .row7(x_row_7));
  DotMatrix #(.inputtype("row"), .matrixcols(8), .matrixrows(8)) dotmatrix_2 (
    .row0(z_row_0), .row1(z_row_1), .row2(z_row_2), .row3(z_row_3), .row4(z_row_4), .row5(z_row_5),
    .row6(z_row_6), .row7(z_row_7));
  matmul matmul_1 (
    .x_row_0(x_row_0), .x_row_1(x_row_1), .x_row_2(x_row_2), .x_row_3(x_row_3), .x_row_4(x_row_4),
    .x_row_5(x_row_5), .x_row_6(x_row_6), .x_row_7(x_row_7), .y_row_0(x_row_0), .y_row_1(x_row_1),
    .y_row_2(x_row_2), .y_row_3(x_row_3), .y_row_4(x_row_4), .y_row_5(x_row_5), .y_row_6(x_row_6),
    .y_row_7(x_row_7), .z_row_0(z_row_0), .z_row_1(z_row_1), .z_row_2(z_row_2), .z_row_3(z_row_3),
    .z_row_4(z_row_4), .z_row_5(z_row_5), .z_row_6(z_row_6), .z_row_7(z_row_7));
endmodule

module pow_3 (
  input  [7:0] x_row_0,
  input  [7:0] x_row_1,
  input  [7:0] x_row_2,
  input  [7:0] x_row_3,
  input  [7:0] x_row_4,
  input  [7:0] x_row_5,
  input  [7:0] x_row_6,
  input  [7:0] x_row_7,
  output [7:0] z_row_0,
  output [7:0] z_row_1,
  output [7:0] z_row_2,
  output [7:0] z_row_3,
  output [7:0] z_row_4,
  output [7:0] z_row_5,
  output [7:0] z_row_6,
  output [7:0] z_row_7
);

  wire [7:0] pow_2_1_z_row_0, pow_2_1_z_row_1, pow_2_1_z_row_2, pow_2_1_z_row_3, pow_2_1_z_row_4,
       pow_2_1_z_row_5, pow_2_1_z_row_6, pow_2_1_z_row_7;

  pow_2 pow_2_1 (
    .x_row_0(x_row_0), .x_row_1(x_row_1), .x_row_2(x_row_2), .x_row_3(x_row_3), .x_row_4(x_row_4),
    .x_row_5(x_row_5), .x_row_6(x_row_6), .x_row_7(x_row_7), .z_row_0(pow_2_1_z_row_0),
    .z_row_1(pow_2_1_z_row_1), .z_row_2(pow_2_1_z_row_2), .z_row_3(pow_2_1_z_row_3),
    .z_row_4(pow_2_1_z_row_4), .z_row_5(pow_2_1_z_row_5), .z_row_6(pow_2_1_z_row_6), .z_row_7(pow_2_1_z_row_7));
  DotMatrix #(.inputtype("row"), .matrixcols(8), .matrixrows(8)) dotmatrix_1 (
    .row0(x_row_0), .row1(x_row_1), .row2(x_row_2), .row3(x_row_3), .row4(x_row_4), .row5(x_row_5),
    .row6(x_row_6), .row7(x_row_7));
  DotMatrix #(.inputtype("row"), .matrixcols(8), .matrixrows(8)) dotmatrix_2 (
    .row0(z_row_0), .row1(z_row_1), .row2(z_row_2), .row3(z_row_3), .row4(z_row_4), .row5(z_row_5),
    .row6(z_row_6), .row7(z_row_7));
  matmul matmul_1 (
    .x_row_0(pow_2_1_z_row_0), .x_row_1(pow_2_1_z_row_1), .x_row_2(pow_2_1_z_row_2),
    .x_row_3(pow_2_1_z_row_3), .x_row_4(pow_2_1_z_row_4), .x_row_5(pow_2_1_z_row_5),
    .x_row_6(pow_2_1_z_row_6), .x_row_7(pow_2_1_z_row_7), .y_row_0(x_row_0), .y_row_1(x_row_1),
    .y_row_2(x_row_2), .y_row_3(x_row_3), .y_row_4(x_row_4), .y_row_5(x_row_5), .y_row_6(x_row_6),
    .y_row_7(x_row_7), .z_row_0(z_row_0), .z_row_1(z_row_1), .z_row_2(z_row_2), .z_row_3(z_row_3),
    .z_row_4(z_row_4), .z_row_5(z_row_5), .z_row_6(z_row_6), .z_row_7(z_row_7));
endmodule

module pow_4 (
  input  [7:0] x_row_0,
  input  [7:0] x_row_1,
  input  [7:0] x_row_2,
  input  [7:0] x_row_3,
  input  [7:0] x_row_4,
  input  [7:0] x_row_5,
  input  [7:0] x_row_6,
  input  [7:0] x_row_7,
  output [7:0] z_row_0,
  output [7:0] z_row_1,
  output [7:0] z_row_2,
  output [7:0] z_row_3,
  output [7:0] z_row_4,
  output [7:0] z_row_5,
  output [7:0] z_row_6,
  output [7:0] z_row_7
);

  wire [7:0] pow_2_1_z_row_0, pow_2_1_z_row_1, pow_2_1_z_row_2, pow_2_1_z_row_3, pow_2_1_z_row_4,
       pow_2_1_z_row_5, pow_2_1_z_row_6, pow_2_1_z_row_7;

  pow_2 pow_2_1 (
    .x_row_0(x_row_0), .x_row_1(x_row_1), .x_row_2(x_row_2), .x_row_3(x_row_3), .x_row_4(x_row_4),
    .x_row_5(x_row_5), .x_row_6(x_row_6), .x_row_7(x_row_7), .z_row_0(pow_2_1_z_row_0),
    .z_row_1(pow_2_1_z_row_1), .z_row_2(pow_2_1_z_row_2), .z_row_3(pow_2_1_z_row_3),
    .z_row_4(pow_2_1_z_row_4), .z_row_5(pow_2_1_z_row_5), .z_row_6(pow_2_1_z_row_6), .z_row_7(pow_2_1_z_row_7));
  pow_2 pow_2_2 (
    .x_row_0(pow_2_1_z_row_0), .x_row_1(pow_2_1_z_row_1), .x_row_2(pow_2_1_z_row_2),
    .x_row_3(pow_2_1_z_row_3), .x_row_4(pow_2_1_z_row_4), .x_row_5(pow_2_1_z_row_5),
    .x_row_6(pow_2_1_z_row_6), .x_row_7(pow_2_1_z_row_7), .z_row_0(z_row_0), .z_row_1(z_row_1),
    .z_row_2(z_row_2), .z_row_3(z_row_3), .z_row_4(z_row_4), .z_row_5(z_row_5), .z_row_6(z_row_6),
    .z_row_7(z_row_7));
  DotMatrix #(.inputtype("row"), .matrixcols(8), .matrixrows(8)) dotmatrix_1 (
    .row0(x_row_0), .row1(x_row_1), .row2(x_row_2), .row3(x_row_3), .row4(x_row_4), .row5(x_row_5),
    .row6(x_row_6), .row7(x_row_7));
  DotMatrix #(.inputtype("row"), .matrixcols(8), .matrixrows(8)) dotmatrix_2 (
    .row0(z_row_0), .row1(z_row_1), .row2(z_row_2), .row3(z_row_3), .row4(z_row_4), .row5(z_row_5),
    .row6(z_row_6), .row7(z_row_7));
endmodule

module pow_5 (
  input  [7:0] x_row_0,
  input  [7:0] x_row_1,
  input  [7:0] x_row_2,
  input  [7:0] x_row_3,
  input  [7:0] x_row_4,
  input  [7:0] x_row_5,
  input  [7:0] x_row_6,
  input  [7:0] x_row_7,
  output [7:0] z_row_0,
  output [7:0] z_row_1,
  output [7:0] z_row_2,
  output [7:0] z_row_3,
  output [7:0] z_row_4,
  output [7:0] z_row_5,
  output [7:0] z_row_6,
  output [7:0] z_row_7
);

  wire [7:0] pow_4_1_z_row_0, pow_4_1_z_row_1, pow_4_1_z_row_2, pow_4_1_z_row_3, pow_4_1_z_row_4,
       pow_4_1_z_row_5, pow_4_1_z_row_6, pow_4_1_z_row_7;

  pow_4 pow_4_1 (
    .x_row_0(x_row_0), .x_row_1(x_row_1), .x_row_2(x_row_2), .x_row_3(x_row_3), .x_row_4(x_row_4),
    .x_row_5(x_row_5), .x_row_6(x_row_6), .x_row_7(x_row_7), .z_row_0(pow_4_1_z_row_0),
    .z_row_1(pow_4_1_z_row_1), .z_row_2(pow_4_1_z_row_2), .z_row_3(pow_4_1_z_row_3),
    .z_row_4(pow_4_1_z_row_4), .z_row_5(pow_4_1_z_row_5), .z_row_6(pow_4_1_z_row_6), .z_row_7(pow_4_1_z_row_7));
  DotMatrix #(.inputtype("row"), .matrixcols(8), .matrixrows(8)) dotmatrix_1 (
    .row0(x_row_0), .row1(x_row_1), .row2(x_row_2), .row3(x_row_3), .row4(x_row_4), .row5(x_row_5),
    .row6(x_row_6), .row7(x_row_7));
  DotMatrix #(.inputtype("row"), .matrixcols(8), .matrixrows(8)) dotmatrix_2 (
    .row0(z_row_0), .row1(z_row_1), .row2(z_row_2), .row3(z_row_3), .row4(z_row_4), .row5(z_row_5),
    .row6(z_row_6), .row7(z_row_7));
  matmul matmul_1 (
    .x_row_0(pow_4_1_z_row_0), .x_row_1(pow_4_1_z_row_1), .x_row_2(pow_4_1_z_row_2),
    .x_row_3(pow_4_1_z_row_3), .x_row_4(pow_4_1_z_row_4), .x_row_5(pow_4_1_z_row_5),
    .x_row_6(pow_4_1_z_row_6), .x_row_7(pow_4_1_z_row_7), .y_row_0(x_row_0), .y_row_1(x_row_1),
    .y_row_2(x_row_2), .y_row_3(x_row_3), .y_row_4(x_row_4), .y_row_5(x_row_5), .y_row_6(x_row_6),
    .y_row_7(x_row_7), .z_row_0(z_row_0), .z_row_1(z_row_1), .z_row_2(z_row_2), .z_row_3(z_row_3),
    .z_row_4(z_row_4), .z_row_5(z_row_5), .z_row_6(z_row_6), .z_row_7(z_row_7));
endmodule

module pow_6 (
  input  [7:0] x_row_0,
  input  [7:0] x_row_1,
  input  [7:0] x_row_2,
  input  [7:0] x_row_3,
  input  [7:0] x_row_4,
  input  [7:0] x_row_5,
  input  [7:0] x_row_6,
  input  [7:0] x_row_7,
  output [7:0] z_row_0,
  output [7:0] z_row_1,
  output [7:0] z_row_2,
  output [7:0] z_row_3,
  output [7:0] z_row_4,
  output [7:0] z_row_5,
  output [7:0] z_row_6,
  output [7:0] z_row_7
);

  wire [7:0] pow_2_1_z_row_0, pow_2_1_z_row_1, pow_2_1_z_row_2, pow_2_1_z_row_3, pow_2_1_z_row_4,
       pow_2_1_z_row_5, pow_2_1_z_row_6, pow_2_1_z_row_7;

  pow_2 pow_2_1 (
    .x_row_0(x_row_0), .x_row_1(x_row_1), .x_row_2(x_row_2), .x_row_3(x_row_3), .x_row_4(x_row_4),
    .x_row_5(x_row_5), .x_row_6(x_row_6), .x_row_7(x_row_7), .z_row_0(pow_2_1_z_row_0),
    .z_row_1(pow_2_1_z_row_1), .z_row_2(pow_2_1_z_row_2), .z_row_3(pow_2_1_z_row_3),
    .z_row_4(pow_2_1_z_row_4), .z_row_5(pow_2_1_z_row_5), .z_row_6(pow_2_1_z_row_6), .z_row_7(pow_2_1_z_row_7));
  pow_3 pow_3_1 (
    .x_row_0(pow_2_1_z_row_0), .x_row_1(pow_2_1_z_row_1), .x_row_2(pow_2_1_z_row_2),
    .x_row_3(pow_2_1_z_row_3), .x_row_4(pow_2_1_z_row_4), .x_row_5(pow_2_1_z_row_5),
    .x_row_6(pow_2_1_z_row_6), .x_row_7(pow_2_1_z_row_7), .z_row_0(z_row_0), .z_row_1(z_row_1),
    .z_row_2(z_row_2), .z_row_3(z_row_3), .z_row_4(z_row_4), .z_row_5(z_row_5), .z_row_6(z_row_6),
    .z_row_7(z_row_7));
  DotMatrix #(.inputtype("row"), .matrixcols(8), .matrixrows(8)) dotmatrix_1 (
    .row0(x_row_0), .row1(x_row_1), .row2(x_row_2), .row3(x_row_3), .row4(x_row_4), .row5(x_row_5),
    .row6(x_row_6), .row7(x_row_7));
  DotMatrix #(.inputtype("row"), .matrixcols(8), .matrixrows(8)) dotmatrix_2 (
    .row0(z_row_0), .row1(z_row_1), .row2(z_row_2), .row3(z_row_3), .row4(z_row_4), .row5(z_row_5),
    .row6(z_row_6), .row7(z_row_7));
endmodule

module pow_7 (
  input  [7:0] x_row_0,
  input  [7:0] x_row_1,
  input  [7:0] x_row_2,
  input  [7:0] x_row_3,
  input  [7:0] x_row_4,
  input  [7:0] x_row_5,
  input  [7:0] x_row_6,
  input  [7:0] x_row_7,
  output [7:0] z_row_0,
  output [7:0] z_row_1,
  output [7:0] z_row_2,
  output [7:0] z_row_3,
  output [7:0] z_row_4,
  output [7:0] z_row_5,
  output [7:0] z_row_6,
  output [7:0] z_row_7
);

  wire [7:0] pow_6_1_z_row_0, pow_6_1_z_row_1, pow_6_1_z_row_2, pow_6_1_z_row_3, pow_6_1_z_row_4,
       pow_6_1_z_row_5, pow_6_1_z_row_6, pow_6_1_z_row_7;

  pow_6 pow_6_1 (
    .x_row_0(x_row_0), .x_row_1(x_row_1), .x_row_2(x_row_2), .x_row_3(x_row_3), .x_row_4(x_row_4),
    .x_row_5(x_row_5), .x_row_6(x_row_6), .x_row_7(x_row_7), .z_row_0(pow_6_1_z_row_0),
    .z_row_1(pow_6_1_z_row_1), .z_row_2(pow_6_1_z_row_2), .z_row_3(pow_6_1_z_row_3),
    .z_row_4(pow_6_1_z_row_4), .z_row_5(pow_6_1_z_row_5), .z_row_6(pow_6_1_z_row_6), .z_row_7(pow_6_1_z_row_7));
  DotMatrix #(.inputtype("row"), .matrixcols(8), .matrixrows(8)) dotmatrix_1 (
    .row0(x_row_0), .row1(x_row_1), .row2(x_row_2), .row3(x_row_3), .row4(x_row_4), .row5(x_row_5),
    .row6(x_row_6), .row7(x_row_7));
  DotMatrix #(.inputtype("row"), .matrixcols(8), .matrixrows(8)) dotmatrix_2 (
    .row0(z_row_0), .row1(z_row_1), .row2(z_row_2), .row3(z_row_3), .row4(z_row_4), .row5(z_row_5),
    .row6(z_row_6), .row7(z_row_7));
  matmul matmul_1 (
    .x_row_0(pow_6_1_z_row_0), .x_row_1(pow_6_1_z_row_1), .x_row_2(pow_6_1_z_row_2),
    .x_row_3(pow_6_1_z_row_3), .x_row_4(pow_6_1_z_row_4), .x_row_5(pow_6_1_z_row_5),
    .x_row_6(pow_6_1_z_row_6), .x_row_7(pow_6_1_z_row_7), .y_row_0(x_row_0), .y_row_1(x_row_1),
    .y_row_2(x_row_2), .y_row_3(x_row_3), .y_row_4(x_row_4), .y_row_5(x_row_5), .y_row_6(x_row_6),
    .y_row_7(x_row_7), .z_row_0(z_row_0), .z_row_1(z_row_1), .z_row_2(z_row_2), .z_row_3(z_row_3),
    .z_row_4(z_row_4), .z_row_5(z_row_5), .z_row_6(z_row_6), .z_row_7(z_row_7));
endmodule

module path_in_exactly_0 (
  input  [7:0] x_row_0,
  input  [7:0] x_row_1,
  input  [7:0] x_row_2,
  input  [7:0] x_row_3,
  input  [7:0] x_row_4,
  input  [7:0] x_row_5,
  input  [7:0] x_row_6,
  input  [7:0] x_row_7,
  input  [2:0] from,
  input  [2:0] to,
  output path_exists
);

  wire [7:0] pow_0_1_z_row_0, pow_0_1_z_row_1, pow_0_1_z_row_2, pow_0_1_z_row_3, pow_0_1_z_row_4,
       pow_0_1_z_row_5, pow_0_1_z_row_6, pow_0_1_z_row_7, row0, z_row_0, z_row_1, z_row_2, z_row_3, z_row_4,
       z_row_5, z_row_6, z_row_7;

  pow_0 pow_0_1 (
    .x_row_0(x_row_0), .x_row_1(x_row_1), .x_row_2(x_row_2), .x_row_3(x_row_3), .x_row_4(x_row_4),
    .x_row_5(x_row_5), .x_row_6(x_row_6), .x_row_7(x_row_7), .z_row_0(pow_0_1_z_row_0),
    .z_row_1(pow_0_1_z_row_1), .z_row_2(pow_0_1_z_row_2), .z_row_3(pow_0_1_z_row_3),
    .z_row_4(pow_0_1_z_row_4), .z_row_5(pow_0_1_z_row_5), .z_row_6(pow_0_1_z_row_6), .z_row_7(pow_0_1_z_row_7));
  DotMatrix #(.inputtype("row"), .matrixcols(8), .matrixrows(8)) dotmatrix_1 (
    .row0(x_row_0), .row1(x_row_1), .row2(x_row_2), .row3(x_row_3), .row4(x_row_4), .row5(x_row_5),
    .row6(x_row_6), .row7(x_row_7));
  DotMatrix #(.inputtype("row"), .matrixcols(8), .matrixrows(8)) dotmatrix_2 (
    .row0(z_row_0), .row1(z_row_1), .row2(z_row_2), .row3(z_row_3), .row4(z_row_4), .row5(z_row_5),
    .row6(z_row_6), .row7(z_row_7));
  Multiplexer #(.select(3), .width(8), .enable("false")) multiplexer_1 (
    .in0(pow_0_1_z_row_0), .in1(pow_0_1_z_row_1), .in2(pow_0_1_z_row_2), .in3(pow_0_1_z_row_3),
    .in4(pow_0_1_z_row_4), .in5(pow_0_1_z_row_5), .in6(pow_0_1_z_row_6), .in7(pow_0_1_z_row_7), .out(row0),
    .sel(from));
  Multiplexer #(.select(3), .enable("false")) multiplexer_2 (
    .in0(row0[7]), .in1(row0[6]), .in2(row0[5]), .in3(row0[4]), .in4(row0[3]), .in5(row0[2]), .in6(row0[1]),
    .in7(row0[0]), .out(path_exists), .sel(to));

  // Other names for the same wires on the sheet: ans0 = path_exists
endmodule

module path_in_exactly_1 (
  input  [7:0] x_row_0,
  input  [7:0] x_row_1,
  input  [7:0] x_row_2,
  input  [7:0] x_row_3,
  input  [7:0] x_row_4,
  input  [7:0] x_row_5,
  input  [7:0] x_row_6,
  input  [7:0] x_row_7,
  input  [2:0] from,
  input  [2:0] to,
  output path_exists
);

  wire [7:0] pow_1_1_z_row_0, pow_1_1_z_row_1, pow_1_1_z_row_2, pow_1_1_z_row_3, pow_1_1_z_row_4,
       pow_1_1_z_row_5, pow_1_1_z_row_6, pow_1_1_z_row_7, row0, z_row_0, z_row_1, z_row_2, z_row_3, z_row_4,
       z_row_5, z_row_6, z_row_7;

  DotMatrix #(.inputtype("row"), .matrixcols(8), .matrixrows(8)) dotmatrix_1 (
    .row0(x_row_0), .row1(x_row_1), .row2(x_row_2), .row3(x_row_3), .row4(x_row_4), .row5(x_row_5),
    .row6(x_row_6), .row7(x_row_7));
  DotMatrix #(.inputtype("row"), .matrixcols(8), .matrixrows(8)) dotmatrix_2 (
    .row0(z_row_0), .row1(z_row_1), .row2(z_row_2), .row3(z_row_3), .row4(z_row_4), .row5(z_row_5),
    .row6(z_row_6), .row7(z_row_7));
  pow_1 pow_1_1 (
    .x_row_0(x_row_0), .x_row_1(x_row_1), .x_row_2(x_row_2), .x_row_3(x_row_3), .x_row_4(x_row_4),
    .x_row_5(x_row_5), .x_row_6(x_row_6), .x_row_7(x_row_7), .z_row_0(pow_1_1_z_row_0),
    .z_row_1(pow_1_1_z_row_1), .z_row_2(pow_1_1_z_row_2), .z_row_3(pow_1_1_z_row_3),
    .z_row_4(pow_1_1_z_row_4), .z_row_5(pow_1_1_z_row_5), .z_row_6(pow_1_1_z_row_6), .z_row_7(pow_1_1_z_row_7));
  Multiplexer #(.select(3), .width(8), .enable("false")) multiplexer_1 (
    .in0(pow_1_1_z_row_0), .in1(pow_1_1_z_row_1), .in2(pow_1_1_z_row_2), .in3(pow_1_1_z_row_3),
    .in4(pow_1_1_z_row_4), .in5(pow_1_1_z_row_5), .in6(pow_1_1_z_row_6), .in7(pow_1_1_z_row_7), .out(row0),
    .sel(from));
  Multiplexer #(.select(3), .enable("false")) multiplexer_2 (
    .in0(row0[7]), .in1(row0[6]), .in2(row0[5]), .in3(row0[4]), .in4(row0[3]), .in5(row0[2]), .in6(row0[1]),
    .in7(row0[0]), .out(path_exists), .sel(to));

  // Other names for the same wires on the sheet: ans0 = path_exists
endmodule

module path_in_exactly_2 (
  input  [7:0] x_row_0,
  input  [7:0] x_row_1,
  input  [7:0] x_row_2,
  input  [7:0] x_row_3,
  input  [7:0] x_row_4,
  input  [7:0] x_row_5,
  input  [7:0] x_row_6,
  input  [7:0] x_row_7,
  input  [2:0] from,
  input  [2:0] to,
  output path_exists
);

  wire [7:0] pow_2_1_z_row_0, pow_2_1_z_row_1, pow_2_1_z_row_2, pow_2_1_z_row_3, pow_2_1_z_row_4,
       pow_2_1_z_row_5, pow_2_1_z_row_6, pow_2_1_z_row_7, row0, z_row_0, z_row_1, z_row_2, z_row_3, z_row_4,
       z_row_5, z_row_6, z_row_7;

  DotMatrix #(.inputtype("row"), .matrixcols(8), .matrixrows(8)) dotmatrix_1 (
    .row0(x_row_0), .row1(x_row_1), .row2(x_row_2), .row3(x_row_3), .row4(x_row_4), .row5(x_row_5),
    .row6(x_row_6), .row7(x_row_7));
  DotMatrix #(.inputtype("row"), .matrixcols(8), .matrixrows(8)) dotmatrix_2 (
    .row0(z_row_0), .row1(z_row_1), .row2(z_row_2), .row3(z_row_3), .row4(z_row_4), .row5(z_row_5),
    .row6(z_row_6), .row7(z_row_7));
  pow_2 pow_2_1 (
    .x_row_0(x_row_0), .x_row_1(x_row_1), .x_row_2(x_row_2), .x_row_3(x_row_3), .x_row_4(x_row_4),
    .x_row_5(x_row_5), .x_row_6(x_row_6), .x_row_7(x_row_7), .z_row_0(pow_2_1_z_row_0),
    .z_row_1(pow_2_1_z_row_1), .z_row_2(pow_2_1_z_row_2), .z_row_3(pow_2_1_z_row_3),
    .z_row_4(pow_2_1_z_row_4), .z_row_5(pow_2_1_z_row_5), .z_row_6(pow_2_1_z_row_6), .z_row_7(pow_2_1_z_row_7));
  Multiplexer #(.select(3), .width(8), .enable("false")) multiplexer_1 (
    .in0(pow_2_1_z_row_0), .in1(pow_2_1_z_row_1), .in2(pow_2_1_z_row_2), .in3(pow_2_1_z_row_3),
    .in4(pow_2_1_z_row_4), .in5(pow_2_1_z_row_5), .in6(pow_2_1_z_row_6), .in7(pow_2_1_z_row_7), .out(row0),
    .sel(from));
  Multiplexer #(.select(3), .enable("false")) multiplexer_2 (
    .in0(row0[7]), .in1(row0[6]), .in2(row0[5]), .in3(row0[4]), .in4(row0[3]), .in5(row0[2]), .in6(row0[1]),
    .in7(row0[0]), .out(path_exists), .sel(to));

  // Other names for the same wires on the sheet: ans0 = path_exists
endmodule

module path_in_exactly_3 (
  input  [7:0] x_row_0,
  input  [7:0] x_row_1,
  input  [7:0] x_row_2,
  input  [7:0] x_row_3,
  input  [7:0] x_row_4,
  input  [7:0] x_row_5,
  input  [7:0] x_row_6,
  input  [7:0] x_row_7,
  input  [2:0] from,
  input  [2:0] to,
  output path_exists
);

  wire [7:0] pow_3_1_z_row_0, pow_3_1_z_row_1, pow_3_1_z_row_2, pow_3_1_z_row_3, pow_3_1_z_row_4,
       pow_3_1_z_row_5, pow_3_1_z_row_6, pow_3_1_z_row_7, row0, z_row_0, z_row_1, z_row_2, z_row_3, z_row_4,
       z_row_5, z_row_6, z_row_7;

  pow_3 pow_3_1 (
    .x_row_0(x_row_0), .x_row_1(x_row_1), .x_row_2(x_row_2), .x_row_3(x_row_3), .x_row_4(x_row_4),
    .x_row_5(x_row_5), .x_row_6(x_row_6), .x_row_7(x_row_7), .z_row_0(pow_3_1_z_row_0),
    .z_row_1(pow_3_1_z_row_1), .z_row_2(pow_3_1_z_row_2), .z_row_3(pow_3_1_z_row_3),
    .z_row_4(pow_3_1_z_row_4), .z_row_5(pow_3_1_z_row_5), .z_row_6(pow_3_1_z_row_6), .z_row_7(pow_3_1_z_row_7));
  DotMatrix #(.inputtype("row"), .matrixcols(8), .matrixrows(8)) dotmatrix_1 (
    .row0(x_row_0), .row1(x_row_1), .row2(x_row_2), .row3(x_row_3), .row4(x_row_4), .row5(x_row_5),
    .row6(x_row_6), .row7(x_row_7));
  DotMatrix #(.inputtype("row"), .matrixcols(8), .matrixrows(8)) dotmatrix_2 (
    .row0(z_row_0), .row1(z_row_1), .row2(z_row_2), .row3(z_row_3), .row4(z_row_4), .row5(z_row_5),
    .row6(z_row_6), .row7(z_row_7));
  Multiplexer #(.select(3), .width(8), .enable("false")) multiplexer_1 (
    .in0(pow_3_1_z_row_0), .in1(pow_3_1_z_row_1), .in2(pow_3_1_z_row_2), .in3(pow_3_1_z_row_3),
    .in4(pow_3_1_z_row_4), .in5(pow_3_1_z_row_5), .in6(pow_3_1_z_row_6), .in7(pow_3_1_z_row_7), .out(row0),
    .sel(from));
  Multiplexer #(.select(3), .enable("false")) multiplexer_2 (
    .in0(row0[7]), .in1(row0[6]), .in2(row0[5]), .in3(row0[4]), .in4(row0[3]), .in5(row0[2]), .in6(row0[1]),
    .in7(row0[0]), .out(path_exists), .sel(to));

  // Other names for the same wires on the sheet: ans0 = path_exists
endmodule

module path_in_exactly_4 (
  input  [7:0] x_row_0,
  input  [7:0] x_row_1,
  input  [7:0] x_row_2,
  input  [7:0] x_row_3,
  input  [7:0] x_row_4,
  input  [7:0] x_row_5,
  input  [7:0] x_row_6,
  input  [7:0] x_row_7,
  input  [2:0] from,
  input  [2:0] to,
  output path_exists
);

  wire [7:0] pow_4_1_z_row_0, pow_4_1_z_row_1, pow_4_1_z_row_2, pow_4_1_z_row_3, pow_4_1_z_row_4,
       pow_4_1_z_row_5, pow_4_1_z_row_6, pow_4_1_z_row_7, row0, z_row_0, z_row_1, z_row_2, z_row_3, z_row_4,
       z_row_5, z_row_6, z_row_7;

  pow_4 pow_4_1 (
    .x_row_0(x_row_0), .x_row_1(x_row_1), .x_row_2(x_row_2), .x_row_3(x_row_3), .x_row_4(x_row_4),
    .x_row_5(x_row_5), .x_row_6(x_row_6), .x_row_7(x_row_7), .z_row_0(pow_4_1_z_row_0),
    .z_row_1(pow_4_1_z_row_1), .z_row_2(pow_4_1_z_row_2), .z_row_3(pow_4_1_z_row_3),
    .z_row_4(pow_4_1_z_row_4), .z_row_5(pow_4_1_z_row_5), .z_row_6(pow_4_1_z_row_6), .z_row_7(pow_4_1_z_row_7));
  DotMatrix #(.inputtype("row"), .matrixcols(8), .matrixrows(8)) dotmatrix_1 (
    .row0(x_row_0), .row1(x_row_1), .row2(x_row_2), .row3(x_row_3), .row4(x_row_4), .row5(x_row_5),
    .row6(x_row_6), .row7(x_row_7));
  DotMatrix #(.inputtype("row"), .matrixcols(8), .matrixrows(8)) dotmatrix_2 (
    .row0(z_row_0), .row1(z_row_1), .row2(z_row_2), .row3(z_row_3), .row4(z_row_4), .row5(z_row_5),
    .row6(z_row_6), .row7(z_row_7));
  Multiplexer #(.select(3), .width(8), .enable("false")) multiplexer_1 (
    .in0(pow_4_1_z_row_0), .in1(pow_4_1_z_row_1), .in2(pow_4_1_z_row_2), .in3(pow_4_1_z_row_3),
    .in4(pow_4_1_z_row_4), .in5(pow_4_1_z_row_5), .in6(pow_4_1_z_row_6), .in7(pow_4_1_z_row_7), .out(row0),
    .sel(from));
  Multiplexer #(.select(3), .enable("false")) multiplexer_2 (
    .in0(row0[7]), .in1(row0[6]), .in2(row0[5]), .in3(row0[4]), .in4(row0[3]), .in5(row0[2]), .in6(row0[1]),
    .in7(row0[0]), .out(path_exists), .sel(to));

  // Other names for the same wires on the sheet: ans0 = path_exists
endmodule

module path_in_exactly_5 (
  input  [7:0] x_row_0,
  input  [7:0] x_row_1,
  input  [7:0] x_row_2,
  input  [7:0] x_row_3,
  input  [7:0] x_row_4,
  input  [7:0] x_row_5,
  input  [7:0] x_row_6,
  input  [7:0] x_row_7,
  input  [2:0] from,
  input  [2:0] to,
  output path_exists
);

  wire [7:0] pow_5_1_z_row_0, pow_5_1_z_row_1, pow_5_1_z_row_2, pow_5_1_z_row_3, pow_5_1_z_row_4,
       pow_5_1_z_row_5, pow_5_1_z_row_6, pow_5_1_z_row_7, row0, z_row_0, z_row_1, z_row_2, z_row_3, z_row_4,
       z_row_5, z_row_6, z_row_7;

  pow_5 pow_5_1 (
    .x_row_0(x_row_0), .x_row_1(x_row_1), .x_row_2(x_row_2), .x_row_3(x_row_3), .x_row_4(x_row_4),
    .x_row_5(x_row_5), .x_row_6(x_row_6), .x_row_7(x_row_7), .z_row_0(pow_5_1_z_row_0),
    .z_row_1(pow_5_1_z_row_1), .z_row_2(pow_5_1_z_row_2), .z_row_3(pow_5_1_z_row_3),
    .z_row_4(pow_5_1_z_row_4), .z_row_5(pow_5_1_z_row_5), .z_row_6(pow_5_1_z_row_6), .z_row_7(pow_5_1_z_row_7));
  DotMatrix #(.inputtype("row"), .matrixcols(8), .matrixrows(8)) dotmatrix_1 (
    .row0(x_row_0), .row1(x_row_1), .row2(x_row_2), .row3(x_row_3), .row4(x_row_4), .row5(x_row_5),
    .row6(x_row_6), .row7(x_row_7));
  DotMatrix #(.inputtype("row"), .matrixcols(8), .matrixrows(8)) dotmatrix_2 (
    .row0(z_row_0), .row1(z_row_1), .row2(z_row_2), .row3(z_row_3), .row4(z_row_4), .row5(z_row_5),
    .row6(z_row_6), .row7(z_row_7));
  Multiplexer #(.select(3), .width(8), .enable("false")) multiplexer_1 (
    .in0(pow_5_1_z_row_0), .in1(pow_5_1_z_row_1), .in2(pow_5_1_z_row_2), .in3(pow_5_1_z_row_3),
    .in4(pow_5_1_z_row_4), .in5(pow_5_1_z_row_5), .in6(pow_5_1_z_row_6), .in7(pow_5_1_z_row_7), .out(row0),
    .sel(from));
  Multiplexer #(.select(3), .enable("false")) multiplexer_2 (
    .in0(row0[7]), .in1(row0[6]), .in2(row0[5]), .in3(row0[4]), .in4(row0[3]), .in5(row0[2]), .in6(row0[1]),
    .in7(row0[0]), .out(path_exists), .sel(to));

  // Other names for the same wires on the sheet: ans0 = path_exists
endmodule

module path_in_exactly_6 (
  input  [7:0] x_row_0,
  input  [7:0] x_row_1,
  input  [7:0] x_row_2,
  input  [7:0] x_row_3,
  input  [7:0] x_row_4,
  input  [7:0] x_row_5,
  input  [7:0] x_row_6,
  input  [7:0] x_row_7,
  input  [2:0] from,
  input  [2:0] to,
  output path_exists
);

  wire [7:0] pow_6_1_z_row_0, pow_6_1_z_row_1, pow_6_1_z_row_2, pow_6_1_z_row_3, pow_6_1_z_row_4,
       pow_6_1_z_row_5, pow_6_1_z_row_6, pow_6_1_z_row_7, row0, z_row_0, z_row_1, z_row_2, z_row_3, z_row_4,
       z_row_5, z_row_6, z_row_7;

  pow_6 pow_6_1 (
    .x_row_0(x_row_0), .x_row_1(x_row_1), .x_row_2(x_row_2), .x_row_3(x_row_3), .x_row_4(x_row_4),
    .x_row_5(x_row_5), .x_row_6(x_row_6), .x_row_7(x_row_7), .z_row_0(pow_6_1_z_row_0),
    .z_row_1(pow_6_1_z_row_1), .z_row_2(pow_6_1_z_row_2), .z_row_3(pow_6_1_z_row_3),
    .z_row_4(pow_6_1_z_row_4), .z_row_5(pow_6_1_z_row_5), .z_row_6(pow_6_1_z_row_6), .z_row_7(pow_6_1_z_row_7));
  DotMatrix #(.inputtype("row"), .matrixcols(8), .matrixrows(8)) dotmatrix_1 (
    .row0(x_row_0), .row1(x_row_1), .row2(x_row_2), .row3(x_row_3), .row4(x_row_4), .row5(x_row_5),
    .row6(x_row_6), .row7(x_row_7));
  DotMatrix #(.inputtype("row"), .matrixcols(8), .matrixrows(8)) dotmatrix_2 (
    .row0(z_row_0), .row1(z_row_1), .row2(z_row_2), .row3(z_row_3), .row4(z_row_4), .row5(z_row_5),
    .row6(z_row_6), .row7(z_row_7));
  Multiplexer #(.select(3), .width(8), .enable("false")) multiplexer_1 (
    .in0(pow_6_1_z_row_0), .in1(pow_6_1_z_row_1), .in2(pow_6_1_z_row_2), .in3(pow_6_1_z_row_3),
    .in4(pow_6_1_z_row_4), .in5(pow_6_1_z_row_5), .in6(pow_6_1_z_row_6), .in7(pow_6_1_z_row_7), .out(row0),
    .sel(from));
  Multiplexer #(.select(3), .enable("false")) multiplexer_2 (
    .in0(row0[7]), .in1(row0[6]), .in2(row0[5]), .in3(row0[4]), .in4(row0[3]), .in5(row0[2]), .in6(row0[1]),
    .in7(row0[0]), .out(path_exists), .sel(to));

  // Other names for the same wires on the sheet: ans0 = path_exists
endmodule

module path_in_exactly_7 (
  input  [7:0] x_row_0,
  input  [7:0] x_row_1,
  input  [7:0] x_row_2,
  input  [7:0] x_row_3,
  input  [7:0] x_row_4,
  input  [7:0] x_row_5,
  input  [7:0] x_row_6,
  input  [7:0] x_row_7,
  input  [2:0] from,
  input  [2:0] to,
  output path_exists
);

  wire [7:0] pow_7_1_z_row_0, pow_7_1_z_row_1, pow_7_1_z_row_2, pow_7_1_z_row_3, pow_7_1_z_row_4,
       pow_7_1_z_row_5, pow_7_1_z_row_6, pow_7_1_z_row_7, row0, z_row_0, z_row_1, z_row_2, z_row_3, z_row_4,
       z_row_5, z_row_6, z_row_7;

  pow_7 pow_7_1 (
    .x_row_0(x_row_0), .z_row_0(pow_7_1_z_row_0), .x_row_1(x_row_1), .z_row_1(pow_7_1_z_row_1),
    .x_row_2(x_row_2), .z_row_2(pow_7_1_z_row_2), .x_row_3(x_row_3), .z_row_3(pow_7_1_z_row_3),
    .x_row_4(x_row_4), .z_row_4(pow_7_1_z_row_4), .x_row_5(x_row_5), .z_row_5(pow_7_1_z_row_5),
    .x_row_6(x_row_6), .z_row_6(pow_7_1_z_row_6), .x_row_7(x_row_7), .z_row_7(pow_7_1_z_row_7));
  DotMatrix #(.inputtype("row"), .matrixcols(8), .matrixrows(8)) dotmatrix_1 (
    .row0(x_row_0), .row1(x_row_1), .row2(x_row_2), .row3(x_row_3), .row4(x_row_4), .row5(x_row_5),
    .row6(x_row_6), .row7(x_row_7));
  DotMatrix #(.inputtype("row"), .matrixcols(8), .matrixrows(8)) dotmatrix_2 (
    .row0(z_row_0), .row1(z_row_1), .row2(z_row_2), .row3(z_row_3), .row4(z_row_4), .row5(z_row_5),
    .row6(z_row_6), .row7(z_row_7));
  Multiplexer #(.select(3), .width(8), .enable("false")) multiplexer_1 (
    .in0(pow_7_1_z_row_0), .in1(pow_7_1_z_row_1), .in2(pow_7_1_z_row_2), .in3(pow_7_1_z_row_3),
    .in4(pow_7_1_z_row_4), .in5(pow_7_1_z_row_5), .in6(pow_7_1_z_row_6), .in7(pow_7_1_z_row_7), .out(row0),
    .sel(from));
  Multiplexer #(.select(3), .enable("false")) multiplexer_2 (
    .in0(row0[7]), .in1(row0[6]), .in2(row0[5]), .in3(row0[4]), .in4(row0[3]), .in5(row0[2]), .in6(row0[1]),
    .in7(row0[0]), .out(path_exists), .sel(to));

  // Other names for the same wires on the sheet: ans0 = path_exists
endmodule

module min_dist_i_j (
  input  [7:0] x_row_0,
  input  [7:0] x_row_1,
  input  [7:0] x_row_2,
  input  [7:0] x_row_3,
  input  [7:0] x_row_4,
  input  [7:0] x_row_5,
  input  [7:0] x_row_6,
  input  [7:0] x_row_7,
  input  [2:0] from,
  input  [2:0] to,
  output path_exists,
  output [2:0] min_dist
);

  wire ans0, ans0_orNone, ans1, ans2, ans3, ans4, ans5, ans6, ans7, not_1_out, or_2_out, or_3_out, or_4_out,
       or_5_out, or_6_out, or_7_out;
  wire [2:0] answer;

  or or_1 (ans0_orNone, ans0, not_1_out);
  not not_1 (not_1_out, path_exists);
  Priority_Encoder #(.disabled(0)) priority_encoder_1 (
    .in0(ans7), .in1(ans6), .in2(ans5), .in3(ans4), .in4(ans3), .in5(ans2), .in6(ans1), .in7(ans0_orNone),
    .out(answer), .en_in(1'b1));  // open: gs, en_out
  path_in_exactly_0 path_in_exactly_0_1 (
    .x_row_0(x_row_0), .x_row_1(x_row_1), .x_row_2(x_row_2), .x_row_3(x_row_3), .x_row_4(x_row_4),
    .x_row_5(x_row_5), .x_row_6(x_row_6), .x_row_7(x_row_7), .from(from), .to(to), .path_exists(ans0));
  path_in_exactly_1 path_in_exactly_1_1 (
    .x_row_0(x_row_0), .x_row_1(x_row_1), .x_row_2(x_row_2), .x_row_3(x_row_3), .x_row_4(x_row_4),
    .x_row_5(x_row_5), .x_row_6(x_row_6), .x_row_7(x_row_7), .from(from), .to(to), .path_exists(ans1));
  path_in_exactly_2 path_in_exactly_2_1 (
    .x_row_0(x_row_0), .x_row_1(x_row_1), .x_row_2(x_row_2), .x_row_3(x_row_3), .x_row_4(x_row_4),
    .x_row_5(x_row_5), .x_row_6(x_row_6), .x_row_7(x_row_7), .from(from), .to(to), .path_exists(ans2));
  path_in_exactly_6 path_in_exactly_6_1 (
    .x_row_0(x_row_0), .x_row_1(x_row_1), .x_row_2(x_row_2), .x_row_3(x_row_3), .x_row_4(x_row_4),
    .x_row_5(x_row_5), .x_row_6(x_row_6), .x_row_7(x_row_7), .from(from), .to(to), .path_exists(ans6));
  // Probe on min_dist
  or or_2 (or_2_out, ans0, ans1);
  or or_3 (or_3_out, ans2, ans3);
  or or_4 (or_4_out, ans4, ans5);
  or or_5 (or_5_out, ans6, ans7);
  or or_6 (or_6_out, or_2_out, or_3_out);
  or or_7 (or_7_out, or_4_out, or_5_out);
  or or_8 (path_exists, or_6_out, or_7_out);
  not not_2 (min_dist[2], answer[2]);
  not not_3 (min_dist[1], answer[1]);
  not not_4 (min_dist[0], answer[0]);
  path_in_exactly_3 path_in_exactly_3_1 (
    .x_row_0(x_row_0), .x_row_1(x_row_1), .x_row_2(x_row_2), .x_row_3(x_row_3), .x_row_4(x_row_4),
    .x_row_5(x_row_5), .x_row_6(x_row_6), .x_row_7(x_row_7), .from(from), .to(to), .path_exists(ans3));
  path_in_exactly_4 path_in_exactly_4_1 (
    .x_row_0(x_row_0), .x_row_1(x_row_1), .x_row_2(x_row_2), .x_row_3(x_row_3), .x_row_4(x_row_4),
    .x_row_5(x_row_5), .x_row_6(x_row_6), .x_row_7(x_row_7), .from(from), .to(to), .path_exists(ans4));
  path_in_exactly_5 path_in_exactly_5_1 (
    .x_row_0(x_row_0), .x_row_1(x_row_1), .x_row_2(x_row_2), .x_row_3(x_row_3), .x_row_4(x_row_4),
    .x_row_5(x_row_5), .x_row_6(x_row_6), .x_row_7(x_row_7), .from(from), .to(to), .path_exists(ans5));
  path_in_exactly_7 path_in_exactly_7_1 (
    .x_row_0(x_row_0), .x_row_1(x_row_1), .x_row_2(x_row_2), .x_row_3(x_row_3), .x_row_4(x_row_4),
    .x_row_5(x_row_5), .x_row_6(x_row_6), .x_row_7(x_row_7), .from(from), .to(to), .path_exists(ans7));

  // Other names for the same wires on the sheet: answer_2 = answer[0]; answer_1 = answer[1]; answer_0 = answer[2];
  //   isthere_path = path_exists
endmodule

module matrix_and_8_8 (
  input  [7:0] x_row_0,
  input  [7:0] x_row_1,
  input  [7:0] x_row_2,
  input  [7:0] x_row_3,
  input  [7:0] x_row_4,
  input  [7:0] x_row_5,
  input  [7:0] x_row_6,
  input  [7:0] x_row_7,
  output z
);

  wire and_1_out, and_2_out, and_3_out, and_4_out, and_5_out, and_6_out, and_7_out, and_8_out, and_9_out,
       and_10_out, and_11_out, and_12_out, and_13_out, and_14_out, and_15_out, and_16_out, and_17_out,
       and_18_out, and_19_out, and_20_out, and_21_out, and_22_out, and_23_out, and_24_out, and_25_out,
       and_26_out, and_27_out, and_28_out, and_29_out, and_30_out, and_31_out, and_32_out, and_33_out,
       and_34_out, and_35_out, and_36_out, and_37_out, and_38_out, and_39_out, and_40_out, and_41_out,
       and_42_out, and_43_out, and_44_out, and_45_out, and_46_out, and_47_out, and_48_out, and_49_out,
       and_50_out, and_51_out, and_52_out, and_53_out, and_54_out, and_55_out, and_56_out, and_57_out,
       and_58_out, and_59_out, and_60_out, and_61_out, and_62_out;
  wire [7:0] z_row_0, z_row_1, z_row_2, z_row_3, z_row_4, z_row_5, z_row_6, z_row_7;

  and and_1 (and_1_out, x_row_0[0], x_row_0[1]);
  and and_2 (and_2_out, x_row_0[2], x_row_0[3]);
  and and_3 (and_3_out, x_row_0[4], x_row_0[5]);
  and and_4 (and_4_out, x_row_0[6], x_row_0[7]);
  and and_5 (and_5_out, x_row_1[0], x_row_1[1]);
  and and_6 (and_6_out, x_row_1[2], x_row_1[3]);
  and and_7 (and_7_out, x_row_1[4], x_row_1[5]);
  and and_8 (and_8_out, x_row_1[6], x_row_1[7]);
  and and_9 (and_9_out, x_row_2[0], x_row_2[1]);
  and and_10 (and_10_out, x_row_2[2], x_row_2[3]);
  and and_11 (and_11_out, x_row_2[4], x_row_2[5]);
  and and_12 (and_12_out, x_row_2[6], x_row_2[7]);
  and and_13 (and_13_out, x_row_3[0], x_row_3[1]);
  and and_14 (and_14_out, x_row_3[2], x_row_3[3]);
  and and_15 (and_15_out, x_row_3[4], x_row_3[5]);
  and and_16 (and_16_out, x_row_3[6], x_row_3[7]);
  and and_17 (and_17_out, x_row_4[0], x_row_4[1]);
  and and_18 (and_18_out, x_row_4[2], x_row_4[3]);
  and and_19 (and_19_out, x_row_4[4], x_row_4[5]);
  and and_20 (and_20_out, x_row_4[6], x_row_4[7]);
  and and_21 (and_21_out, x_row_5[0], x_row_5[1]);
  and and_22 (and_22_out, x_row_5[2], x_row_5[3]);
  and and_23 (and_23_out, x_row_5[4], x_row_5[5]);
  and and_24 (and_24_out, x_row_5[6], x_row_5[7]);
  and and_25 (and_25_out, x_row_6[0], x_row_6[1]);
  and and_26 (and_26_out, x_row_6[2], x_row_6[3]);
  and and_27 (and_27_out, x_row_6[4], x_row_6[5]);
  and and_28 (and_28_out, x_row_6[6], x_row_6[7]);
  and and_29 (and_29_out, x_row_7[0], x_row_7[1]);
  and and_30 (and_30_out, x_row_7[2], x_row_7[3]);
  and and_31 (and_31_out, x_row_7[4], x_row_7[5]);
  and and_32 (and_32_out, x_row_7[6], x_row_7[7]);
  DotMatrix #(.inputtype("row"), .matrixcols(8), .matrixrows(8)) dotmatrix_1 (
    .row0(x_row_0), .row1(x_row_1), .row2(x_row_2), .row3(x_row_3), .row4(x_row_4), .row5(x_row_5),
    .row6(x_row_6), .row7(x_row_7));
  and and_33 (and_33_out, and_1_out, and_2_out);
  and and_34 (and_34_out, and_3_out, and_4_out);
  and and_35 (and_35_out, and_5_out, and_6_out);
  and and_36 (and_36_out, and_7_out, and_8_out);
  and and_37 (and_37_out, and_9_out, and_10_out);
  and and_38 (and_38_out, and_11_out, and_12_out);
  and and_39 (and_39_out, and_13_out, and_14_out);
  and and_40 (and_40_out, and_15_out, and_16_out);
  and and_41 (and_41_out, and_17_out, and_18_out);
  and and_42 (and_42_out, and_19_out, and_20_out);
  and and_43 (and_43_out, and_21_out, and_22_out);
  and and_44 (and_44_out, and_23_out, and_24_out);
  and and_45 (and_45_out, and_25_out, and_26_out);
  and and_46 (and_46_out, and_27_out, and_28_out);
  and and_47 (and_47_out, and_29_out, and_30_out);
  and and_48 (and_48_out, and_31_out, and_32_out);
  and and_49 (and_49_out, and_33_out, and_34_out);
  and and_50 (and_50_out, and_35_out, and_36_out);
  and and_51 (and_51_out, and_37_out, and_38_out);
  and and_52 (and_52_out, and_39_out, and_40_out);
  and and_53 (and_53_out, and_41_out, and_42_out);
  and and_54 (and_54_out, and_43_out, and_44_out);
  and and_55 (and_55_out, and_45_out, and_46_out);
  and and_56 (and_56_out, and_47_out, and_48_out);
  and and_57 (and_57_out, and_49_out, and_50_out);
  and and_58 (and_58_out, and_51_out, and_52_out);
  and and_59 (and_59_out, and_53_out, and_54_out);
  and and_60 (and_60_out, and_55_out, and_56_out);
  DotMatrix #(.inputtype("row"), .matrixcols(8), .matrixrows(8)) dotmatrix_2 (
    .row0(z_row_0), .row1(z_row_1), .row2(z_row_2), .row3(z_row_3), .row4(z_row_4), .row5(z_row_5),
    .row6(z_row_6), .row7(z_row_7));
  and and_61 (and_61_out, and_59_out, and_60_out);
  and and_62 (and_62_out, and_57_out, and_58_out);
  and and_63 (z, and_62_out, and_61_out);

  // Other names for the same wires on the sheet: x00 = x_row_0[0]; x01 = x_row_0[1]; x02 = x_row_0[2];
  //   x03 = x_row_0[3]; x04 = x_row_0[4]; x05 = x_row_0[5]; x06 = x_row_0[6]; x07 = x_row_0[7]; x10 = x_row_1[0];
  //   x11 = x_row_1[1]; x12 = x_row_1[2]; x13 = x_row_1[3]; x14 = x_row_1[4]; x15 = x_row_1[5]; x16 = x_row_1[6];
  //   x17 = x_row_1[7]; x20 = x_row_2[0]; x21 = x_row_2[1]; x22 = x_row_2[2]; x23 = x_row_2[3]; x24 = x_row_2[4];
  //   x25 = x_row_2[5]; x26 = x_row_2[6]; x27 = x_row_2[7]; x30 = x_row_3[0]; x31 = x_row_3[1]; x32 = x_row_3[2];
  //   x33 = x_row_3[3]; x34 = x_row_3[4]; x35 = x_row_3[5]; x36 = x_row_3[6]; x37 = x_row_3[7]; x40 = x_row_4[0];
  //   x41 = x_row_4[1]; x42 = x_row_4[2]; x43 = x_row_4[3]; x44 = x_row_4[4]; x45 = x_row_4[5]; x46 = x_row_4[6];
  //   x47 = x_row_4[7]; x50 = x_row_5[0]; x51 = x_row_5[1]; x52 = x_row_5[2]; x53 = x_row_5[3]; x54 = x_row_5[4];
  //   x55 = x_row_5[5]; x56 = x_row_5[6]; x57 = x_row_5[7]; x60 = x_row_6[0]; x61 = x_row_6[1]; x62 = x_row_6[2];
  //   x63 = x_row_6[3]; x64 = x_row_6[4]; x65 = x_row_6[5]; x66 = x_row_6[6]; x67 = x_row_6[7]; x70 = x_row_7[0];
  //   x71 = x_row_7[1]; x72 = x_row_7[2]; x73 = x_row_7[3]; x74 = x_row_7[4]; x75 = x_row_7[5]; x76 = x_row_7[6];
  //   x77 = x_row_7[7]
endmodule

module min_dist_anywhere (
  input  [7:0] x_row_0,
  input  [7:0] x_row_1,
  input  [7:0] x_row_2,
  input  [7:0] x_row_3,
  input  [7:0] x_row_4,
  input  [7:0] x_row_5,
  input  [7:0] x_row_6,
  input  [7:0] x_row_7,
  output path_exists,
  output [2:0] min_dist
);

  wire ANS0, ans0_orNone, ANS1, ANS2, ANS3, ANS4, ANS5, ANS6, ANS7, not_1_out, or_2_out, or_3_out, or_4_out,
       or_5_out, or_6_out, or_7_out;
  wire [2:0] answer;
  wire [7:0] pow_0_1_z_row_0, pow_0_1_z_row_1, pow_0_1_z_row_2, pow_0_1_z_row_3, pow_0_1_z_row_4,
       pow_0_1_z_row_5, pow_0_1_z_row_6, pow_0_1_z_row_7, pow_1_1_z_row_0, pow_1_1_z_row_1, pow_1_1_z_row_2,
       pow_1_1_z_row_3, pow_1_1_z_row_4, pow_1_1_z_row_5, pow_1_1_z_row_6, pow_1_1_z_row_7, pow_2_1_z_row_0,
       pow_2_1_z_row_1, pow_2_1_z_row_2, pow_2_1_z_row_3, pow_2_1_z_row_4, pow_2_1_z_row_5, pow_2_1_z_row_6,
       pow_2_1_z_row_7, pow_3_1_z_row_0, pow_3_1_z_row_1, pow_3_1_z_row_2, pow_3_1_z_row_3, pow_3_1_z_row_4,
       pow_3_1_z_row_5, pow_3_1_z_row_6, pow_3_1_z_row_7, pow_4_1_z_row_0, pow_4_1_z_row_1, pow_4_1_z_row_2,
       pow_4_1_z_row_3, pow_4_1_z_row_4, pow_4_1_z_row_5, pow_4_1_z_row_6, pow_4_1_z_row_7, pow_5_1_z_row_0,
       pow_5_1_z_row_1, pow_5_1_z_row_2, pow_5_1_z_row_3, pow_5_1_z_row_4, pow_5_1_z_row_5, pow_5_1_z_row_6,
       pow_5_1_z_row_7, pow_6_1_z_row_0, pow_6_1_z_row_1, pow_6_1_z_row_2, pow_6_1_z_row_3, pow_6_1_z_row_4,
       pow_6_1_z_row_5, pow_6_1_z_row_6, pow_6_1_z_row_7, pow_7_1_z_row_0, pow_7_1_z_row_1, pow_7_1_z_row_2,
       pow_7_1_z_row_3, pow_7_1_z_row_4, pow_7_1_z_row_5, pow_7_1_z_row_6, pow_7_1_z_row_7;

  pow_0 pow_0_1 (
    .x_row_0(x_row_0), .x_row_1(x_row_1), .x_row_2(x_row_2), .x_row_3(x_row_3), .x_row_4(x_row_4),
    .x_row_5(x_row_5), .x_row_6(x_row_6), .x_row_7(x_row_7), .z_row_0(pow_0_1_z_row_0),
    .z_row_1(pow_0_1_z_row_1), .z_row_2(pow_0_1_z_row_2), .z_row_3(pow_0_1_z_row_3),
    .z_row_4(pow_0_1_z_row_4), .z_row_5(pow_0_1_z_row_5), .z_row_6(pow_0_1_z_row_6), .z_row_7(pow_0_1_z_row_7));
  pow_1 pow_1_1 (
    .x_row_0(x_row_0), .x_row_1(x_row_1), .x_row_2(x_row_2), .x_row_3(x_row_3), .x_row_4(x_row_4),
    .x_row_5(x_row_5), .x_row_6(x_row_6), .x_row_7(x_row_7), .z_row_0(pow_1_1_z_row_0),
    .z_row_1(pow_1_1_z_row_1), .z_row_2(pow_1_1_z_row_2), .z_row_3(pow_1_1_z_row_3),
    .z_row_4(pow_1_1_z_row_4), .z_row_5(pow_1_1_z_row_5), .z_row_6(pow_1_1_z_row_6), .z_row_7(pow_1_1_z_row_7));
  pow_2 pow_2_1 (
    .x_row_0(x_row_0), .x_row_1(x_row_1), .x_row_2(x_row_2), .x_row_3(x_row_3), .x_row_4(x_row_4),
    .x_row_5(x_row_5), .x_row_6(x_row_6), .x_row_7(x_row_7), .z_row_0(pow_2_1_z_row_0),
    .z_row_1(pow_2_1_z_row_1), .z_row_2(pow_2_1_z_row_2), .z_row_3(pow_2_1_z_row_3),
    .z_row_4(pow_2_1_z_row_4), .z_row_5(pow_2_1_z_row_5), .z_row_6(pow_2_1_z_row_6), .z_row_7(pow_2_1_z_row_7));
  pow_3 pow_3_1 (
    .x_row_0(x_row_0), .x_row_1(x_row_1), .x_row_2(x_row_2), .x_row_3(x_row_3), .x_row_4(x_row_4),
    .x_row_5(x_row_5), .x_row_6(x_row_6), .x_row_7(x_row_7), .z_row_0(pow_3_1_z_row_0),
    .z_row_1(pow_3_1_z_row_1), .z_row_2(pow_3_1_z_row_2), .z_row_3(pow_3_1_z_row_3),
    .z_row_4(pow_3_1_z_row_4), .z_row_5(pow_3_1_z_row_5), .z_row_6(pow_3_1_z_row_6), .z_row_7(pow_3_1_z_row_7));
  matrix_and_8_8 matrix_and_8_8_1 (
    .x_row_0(pow_0_1_z_row_0), .x_row_1(pow_0_1_z_row_1), .x_row_2(pow_0_1_z_row_2),
    .x_row_3(pow_0_1_z_row_3), .x_row_4(pow_0_1_z_row_4), .x_row_5(pow_0_1_z_row_5),
    .x_row_6(pow_0_1_z_row_6), .x_row_7(pow_0_1_z_row_7), .z(ANS0));
  matrix_and_8_8 matrix_and_8_8_2 (
    .x_row_0(pow_1_1_z_row_0), .x_row_1(pow_1_1_z_row_1), .x_row_2(pow_1_1_z_row_2),
    .x_row_3(pow_1_1_z_row_3), .x_row_4(pow_1_1_z_row_4), .x_row_5(pow_1_1_z_row_5),
    .x_row_6(pow_1_1_z_row_6), .x_row_7(pow_1_1_z_row_7), .z(ANS1));
  matrix_and_8_8 matrix_and_8_8_3 (
    .x_row_0(pow_2_1_z_row_0), .x_row_1(pow_2_1_z_row_1), .x_row_2(pow_2_1_z_row_2),
    .x_row_3(pow_2_1_z_row_3), .x_row_4(pow_2_1_z_row_4), .x_row_5(pow_2_1_z_row_5),
    .x_row_6(pow_2_1_z_row_6), .x_row_7(pow_2_1_z_row_7), .z(ANS2));
  matrix_and_8_8 matrix_and_8_8_4 (
    .x_row_0(pow_3_1_z_row_0), .x_row_1(pow_3_1_z_row_1), .x_row_2(pow_3_1_z_row_2),
    .x_row_3(pow_3_1_z_row_3), .x_row_4(pow_3_1_z_row_4), .x_row_5(pow_3_1_z_row_5),
    .x_row_6(pow_3_1_z_row_6), .x_row_7(pow_3_1_z_row_7), .z(ANS3));
  or or_1 (ans0_orNone, ANS0, not_1_out);
  not not_1 (not_1_out, path_exists);
  or or_2 (or_2_out, ANS0, ANS1);
  or or_3 (or_3_out, ANS2, ANS3);
  or or_4 (or_4_out, ANS4, ANS5);
  or or_5 (or_5_out, ANS6, ANS7);
  // Probe on min_dist
  or or_6 (or_6_out, or_2_out, or_3_out);
  or or_7 (or_7_out, or_4_out, or_5_out);
  or or_8 (path_exists, or_6_out, or_7_out);
  pow_4 pow_4_1 (
    .x_row_0(x_row_0), .x_row_1(x_row_1), .x_row_2(x_row_2), .x_row_3(x_row_3), .x_row_4(x_row_4),
    .x_row_5(x_row_5), .x_row_6(x_row_6), .x_row_7(x_row_7), .z_row_0(pow_4_1_z_row_0),
    .z_row_1(pow_4_1_z_row_1), .z_row_2(pow_4_1_z_row_2), .z_row_3(pow_4_1_z_row_3),
    .z_row_4(pow_4_1_z_row_4), .z_row_5(pow_4_1_z_row_5), .z_row_6(pow_4_1_z_row_6), .z_row_7(pow_4_1_z_row_7));
  pow_5 pow_5_1 (
    .x_row_0(x_row_0), .x_row_1(x_row_1), .x_row_2(x_row_2), .x_row_3(x_row_3), .x_row_4(x_row_4),
    .x_row_5(x_row_5), .x_row_6(x_row_6), .x_row_7(x_row_7), .z_row_0(pow_5_1_z_row_0),
    .z_row_1(pow_5_1_z_row_1), .z_row_2(pow_5_1_z_row_2), .z_row_3(pow_5_1_z_row_3),
    .z_row_4(pow_5_1_z_row_4), .z_row_5(pow_5_1_z_row_5), .z_row_6(pow_5_1_z_row_6), .z_row_7(pow_5_1_z_row_7));
  pow_6 pow_6_1 (
    .x_row_0(x_row_0), .x_row_1(x_row_1), .x_row_2(x_row_2), .x_row_3(x_row_3), .x_row_4(x_row_4),
    .x_row_5(x_row_5), .x_row_6(x_row_6), .x_row_7(x_row_7), .z_row_0(pow_6_1_z_row_0),
    .z_row_1(pow_6_1_z_row_1), .z_row_2(pow_6_1_z_row_2), .z_row_3(pow_6_1_z_row_3),
    .z_row_4(pow_6_1_z_row_4), .z_row_5(pow_6_1_z_row_5), .z_row_6(pow_6_1_z_row_6), .z_row_7(pow_6_1_z_row_7));
  pow_7 pow_7_1 (
    .x_row_0(x_row_0), .z_row_0(pow_7_1_z_row_0), .x_row_1(x_row_1), .z_row_1(pow_7_1_z_row_1),
    .x_row_2(x_row_2), .z_row_2(pow_7_1_z_row_2), .x_row_3(x_row_3), .z_row_3(pow_7_1_z_row_3),
    .x_row_4(x_row_4), .z_row_4(pow_7_1_z_row_4), .x_row_5(x_row_5), .z_row_5(pow_7_1_z_row_5),
    .x_row_6(x_row_6), .z_row_6(pow_7_1_z_row_6), .x_row_7(x_row_7), .z_row_7(pow_7_1_z_row_7));
  Priority_Encoder #(.disabled(0)) priority_encoder_1 (
    .in0(ANS7), .in1(ANS6), .in2(ANS5), .in3(ANS4), .in4(ANS3), .in5(ANS2), .in6(ANS1), .in7(ans0_orNone),
    .out(answer), .en_in(1'b1));  // open: gs, en_out
  matrix_and_8_8 matrix_and_8_8_5 (
    .x_row_0(pow_4_1_z_row_0), .x_row_1(pow_4_1_z_row_1), .x_row_2(pow_4_1_z_row_2),
    .x_row_3(pow_4_1_z_row_3), .x_row_4(pow_4_1_z_row_4), .x_row_5(pow_4_1_z_row_5),
    .x_row_6(pow_4_1_z_row_6), .x_row_7(pow_4_1_z_row_7), .z(ANS4));
  matrix_and_8_8 matrix_and_8_8_6 (
    .x_row_0(pow_5_1_z_row_0), .x_row_1(pow_5_1_z_row_1), .x_row_2(pow_5_1_z_row_2),
    .x_row_3(pow_5_1_z_row_3), .x_row_4(pow_5_1_z_row_4), .x_row_5(pow_5_1_z_row_5),
    .x_row_6(pow_5_1_z_row_6), .x_row_7(pow_5_1_z_row_7), .z(ANS5));
  matrix_and_8_8 matrix_and_8_8_7 (
    .x_row_0(pow_6_1_z_row_0), .x_row_1(pow_6_1_z_row_1), .x_row_2(pow_6_1_z_row_2),
    .x_row_3(pow_6_1_z_row_3), .x_row_4(pow_6_1_z_row_4), .x_row_5(pow_6_1_z_row_5),
    .x_row_6(pow_6_1_z_row_6), .x_row_7(pow_6_1_z_row_7), .z(ANS6));
  matrix_and_8_8 matrix_and_8_8_8 (
    .x_row_0(pow_7_1_z_row_0), .x_row_1(pow_7_1_z_row_1), .x_row_2(pow_7_1_z_row_2),
    .x_row_3(pow_7_1_z_row_3), .x_row_4(pow_7_1_z_row_4), .x_row_5(pow_7_1_z_row_5),
    .x_row_6(pow_7_1_z_row_6), .x_row_7(pow_7_1_z_row_7), .z(ANS7));
  not not_2 (min_dist[2], answer[2]);
  not not_3 (min_dist[1], answer[1]);
  not not_4 (min_dist[0], answer[0]);

  // Other names for the same wires on the sheet: answer_2 = answer[0]; answer_1 = answer[1]; answer_0 = answer[2];
  //   isthere_path = path_exists
endmodule

module exactly (
  input  [7:0] x_row_0,
  input  [7:0] x_row_1,
  input  [7:0] x_row_2,
  input  [7:0] x_row_3,
  input  [7:0] x_row_4,
  input  [7:0] x_row_5,
  input  [7:0] x_row_6,
  input  [7:0] x_row_7,
  input  [2:0] from,
  input  [2:0] to,
  input  [2:0] num_steps,
  output path_exists
);

  wire ans0, ans1, ans2, ans3, ans4, ans5, ans6, ans7;

  DotMatrix #(.inputtype("row"), .matrixcols(8), .matrixrows(8)) dotmatrix_1 (
    .row0(x_row_0), .row1(x_row_1), .row2(x_row_2), .row3(x_row_3), .row4(x_row_4), .row5(x_row_5),
    .row6(x_row_6), .row7(x_row_7));
  path_in_exactly_0 path_in_exactly_0_1 (
    .x_row_0(x_row_0), .x_row_1(x_row_1), .x_row_2(x_row_2), .x_row_3(x_row_3), .x_row_4(x_row_4),
    .x_row_5(x_row_5), .x_row_6(x_row_6), .x_row_7(x_row_7), .from(from), .to(to), .path_exists(ans0));
  path_in_exactly_1 path_in_exactly_1_1 (
    .x_row_0(x_row_0), .x_row_1(x_row_1), .x_row_2(x_row_2), .x_row_3(x_row_3), .x_row_4(x_row_4),
    .x_row_5(x_row_5), .x_row_6(x_row_6), .x_row_7(x_row_7), .from(from), .to(to), .path_exists(ans1));
  path_in_exactly_2 path_in_exactly_2_1 (
    .x_row_0(x_row_0), .x_row_1(x_row_1), .x_row_2(x_row_2), .x_row_3(x_row_3), .x_row_4(x_row_4),
    .x_row_5(x_row_5), .x_row_6(x_row_6), .x_row_7(x_row_7), .from(from), .to(to), .path_exists(ans2));
  path_in_exactly_6 path_in_exactly_6_1 (
    .x_row_0(x_row_0), .x_row_1(x_row_1), .x_row_2(x_row_2), .x_row_3(x_row_3), .x_row_4(x_row_4),
    .x_row_5(x_row_5), .x_row_6(x_row_6), .x_row_7(x_row_7), .from(from), .to(to), .path_exists(ans6));
  path_in_exactly_3 path_in_exactly_3_1 (
    .x_row_0(x_row_0), .x_row_1(x_row_1), .x_row_2(x_row_2), .x_row_3(x_row_3), .x_row_4(x_row_4),
    .x_row_5(x_row_5), .x_row_6(x_row_6), .x_row_7(x_row_7), .from(from), .to(to), .path_exists(ans3));
  path_in_exactly_4 path_in_exactly_4_1 (
    .x_row_0(x_row_0), .x_row_1(x_row_1), .x_row_2(x_row_2), .x_row_3(x_row_3), .x_row_4(x_row_4),
    .x_row_5(x_row_5), .x_row_6(x_row_6), .x_row_7(x_row_7), .from(from), .to(to), .path_exists(ans4));
  path_in_exactly_5 path_in_exactly_5_1 (
    .x_row_0(x_row_0), .x_row_1(x_row_1), .x_row_2(x_row_2), .x_row_3(x_row_3), .x_row_4(x_row_4),
    .x_row_5(x_row_5), .x_row_6(x_row_6), .x_row_7(x_row_7), .from(from), .to(to), .path_exists(ans5));
  path_in_exactly_7 path_in_exactly_7_1 (
    .x_row_0(x_row_0), .x_row_1(x_row_1), .x_row_2(x_row_2), .x_row_3(x_row_3), .x_row_4(x_row_4),
    .x_row_5(x_row_5), .x_row_6(x_row_6), .x_row_7(x_row_7), .from(from), .to(to), .path_exists(ans7));
  Multiplexer #(.select(3), .enable("false")) multiplexer_1 (
    .in0(ans0), .in1(ans1), .in2(ans2), .in3(ans3), .in4(ans4), .in5(ans5), .in6(ans6), .in7(ans7),
    .out(path_exists), .sel(num_steps));
endmodule

module atmost (
  input  [7:0] x_row_0,
  input  [7:0] x_row_1,
  input  [7:0] x_row_2,
  input  [7:0] x_row_3,
  input  [7:0] x_row_4,
  input  [7:0] x_row_5,
  input  [7:0] x_row_6,
  input  [7:0] x_row_7,
  input  [2:0] from,
  input  [2:0] to,
  input  [2:0] num_steps,
  output path_exists
);

  wire and_1_out, and_2_out, and_3_out, and_4_out, and_5_out, and_6_out, and_7_out, and_8_out, and_9_out,
       and_10_out, and_11_out, and_12_out, and_13_out, ans0, ans1, ans2, ans3, ans4, ans5, ans6, ans7,
       or_1_out, or_2_out, or_3_out, or_4_out, or_5_out, or_6_out, or_7_out, or_8_out, or_9_out, or_10_out,
       or_11_out;

  DotMatrix #(.inputtype("row"), .matrixcols(8), .matrixrows(8)) dotmatrix_1 (
    .row0(x_row_0), .row1(x_row_1), .row2(x_row_2), .row3(x_row_3), .row4(x_row_4), .row5(x_row_5),
    .row6(x_row_6), .row7(x_row_7));
  path_in_exactly_0 path_in_exactly_0_1 (
    .x_row_0(x_row_0), .x_row_1(x_row_1), .x_row_2(x_row_2), .x_row_3(x_row_3), .x_row_4(x_row_4),
    .x_row_5(x_row_5), .x_row_6(x_row_6), .x_row_7(x_row_7), .from(from), .to(to), .path_exists(ans0));
  path_in_exactly_1 path_in_exactly_1_1 (
    .x_row_0(x_row_0), .x_row_1(x_row_1), .x_row_2(x_row_2), .x_row_3(x_row_3), .x_row_4(x_row_4),
    .x_row_5(x_row_5), .x_row_6(x_row_6), .x_row_7(x_row_7), .from(from), .to(to), .path_exists(ans1));
  path_in_exactly_2 path_in_exactly_2_1 (
    .x_row_0(x_row_0), .x_row_1(x_row_1), .x_row_2(x_row_2), .x_row_3(x_row_3), .x_row_4(x_row_4),
    .x_row_5(x_row_5), .x_row_6(x_row_6), .x_row_7(x_row_7), .from(from), .to(to), .path_exists(ans2));
  path_in_exactly_6 path_in_exactly_6_1 (
    .x_row_0(x_row_0), .x_row_1(x_row_1), .x_row_2(x_row_2), .x_row_3(x_row_3), .x_row_4(x_row_4),
    .x_row_5(x_row_5), .x_row_6(x_row_6), .x_row_7(x_row_7), .from(from), .to(to), .path_exists(ans6));
  path_in_exactly_3 path_in_exactly_3_1 (
    .x_row_0(x_row_0), .x_row_1(x_row_1), .x_row_2(x_row_2), .x_row_3(x_row_3), .x_row_4(x_row_4),
    .x_row_5(x_row_5), .x_row_6(x_row_6), .x_row_7(x_row_7), .from(from), .to(to), .path_exists(ans3));
  path_in_exactly_4 path_in_exactly_4_1 (
    .x_row_0(x_row_0), .x_row_1(x_row_1), .x_row_2(x_row_2), .x_row_3(x_row_3), .x_row_4(x_row_4),
    .x_row_5(x_row_5), .x_row_6(x_row_6), .x_row_7(x_row_7), .from(from), .to(to), .path_exists(ans4));
  path_in_exactly_5 path_in_exactly_5_1 (
    .x_row_0(x_row_0), .x_row_1(x_row_1), .x_row_2(x_row_2), .x_row_3(x_row_3), .x_row_4(x_row_4),
    .x_row_5(x_row_5), .x_row_6(x_row_6), .x_row_7(x_row_7), .from(from), .to(to), .path_exists(ans5));
  path_in_exactly_7 path_in_exactly_7_1 (
    .x_row_0(x_row_0), .x_row_1(x_row_1), .x_row_2(x_row_2), .x_row_3(x_row_3), .x_row_4(x_row_4),
    .x_row_5(x_row_5), .x_row_6(x_row_6), .x_row_7(x_row_7), .from(from), .to(to), .path_exists(ans7));
  and and_1 (and_1_out, num_steps[1], num_steps[2]);
  and and_2 (and_2_out, num_steps[2], num_steps[1]);
  and and_3 (and_3_out, num_steps[2], num_steps[1]);
  and and_4 (and_4_out, num_steps[2], num_steps[0]);
  and and_5 (and_5_out, num_steps[0], num_steps[1]);
  or or_1 (or_1_out, num_steps[2], num_steps[1]);
  and and_6 (and_6_out, and_1_out, num_steps[0]);
  and and_7 (and_7_out, and_2_out, ans6);
  or or_2 (or_2_out, and_3_out, and_4_out);
  or or_3 (or_3_out, and_5_out, num_steps[2]);
  or or_4 (or_4_out, num_steps[2], num_steps[1]);
  and and_8 (and_8_out, and_6_out, ans7);
  and and_9 (and_9_out, ans3, or_3_out);
  or or_5 (or_5_out, num_steps[0], or_1_out);
  and and_10 (and_10_out, or_4_out, ans2);
  and and_11 (and_11_out, num_steps[2], ans4);
  and and_12 (and_12_out, or_2_out, ans5);
  and and_13 (and_13_out, ans1, or_5_out);
  or or_6 (or_6_out, and_8_out, and_7_out);
  or or_7 (or_7_out, and_12_out, and_9_out);
  or or_8 (or_8_out, and_10_out, and_11_out);
  or or_9 (or_9_out, and_13_out, ans0);
  or or_10 (or_10_out, or_6_out, or_7_out);
  or or_11 (or_11_out, or_9_out, or_8_out);
  or or_12 (path_exists, or_10_out, or_11_out);

  // Other names for the same wires on the sheet: ns_0 = num_steps[0]; ns_1 = num_steps[1]; ns_2 = num_steps[2]
endmodule
